// Logisim project Calculator.circ as structural Verilog: 21 circuits, main circuit calculate
module main (
);

  wire button_1_out, button_2_out, button_3_out, button_4_out, button_5_out, button_6_out, button_7_out,
       button_8_out, button_9_out, button_10_out, button_11_out, button_12_out, button_13_out, button_14_out,
       button_15_out, button_16_out, calculate_1_erorr, calculate_1_m, calculate_1_mul, calculate_1_out_27,
       calculate_1_p;
  wire [3:0] calculate_1_out_21, calculate_1_out_22, calculate_1_out_23, calculate_1_out_24,
       calculate_1_out_25, calculate_1_out_26;

  _7_Segment_Display u_7_segment_display_1 (.d(calculate_1_out_27));  // open: g, f, a, b, e, c, dp
  calculate calculate_1 (
    .in_16(button_16_out), .in_4(button_13_out), .in_8(button_14_out), .in_12(button_15_out),
    .in_2(button_1_out), .in_6(button_2_out), .in_10(button_3_out), .in_14(button_4_out),
    .in_3(button_5_out), .in_7(button_7_out), .in_11(button_9_out), .in_15(button_11_out),
    .in_1(button_6_out), .in_5(button_8_out), .in_9(button_10_out), .in_13(button_12_out),
    .out_27(calculate_1_out_27), .out_26(calculate_1_out_26), .out_25(calculate_1_out_25),
    .out_24(calculate_1_out_24), .out_23(calculate_1_out_23), .out_22(calculate_1_out_22),
    .out_21(calculate_1_out_21), .ERORR(calculate_1_erorr), .P(calculate_1_p), .MUL(calculate_1_mul),
    .M(calculate_1_m));
  Hex_Digit_Display hex_digit_display_1 (.value(calculate_1_out_26));  // open: dp
  Hex_Digit_Display hex_digit_display_2 (.value(calculate_1_out_25));  // open: dp
  Hex_Digit_Display hex_digit_display_3 (.value(calculate_1_out_24));  // open: dp
  Hex_Digit_Display hex_digit_display_4 (.value(calculate_1_out_23));  // open: dp
  Hex_Digit_Display hex_digit_display_5 (.value(calculate_1_out_22));  // open: dp
  Hex_Digit_Display hex_digit_display_6 (.value(calculate_1_out_21));  // open: dp
  LED led_1 (.in(calculate_1_erorr));
  LED led_2 (.in(calculate_1_p));
  LED led_3 (.in(calculate_1_m));
  LED led_4 (.in(calculate_1_mul));
  Button button_1 (.out(button_1_out));
  Button button_2 (.out(button_2_out));
  Button button_3 (.out(button_3_out));
  Button button_4 (.out(button_4_out));
  Button button_5 (.out(button_5_out));
  Button button_6 (.out(button_6_out));
  Button button_7 (.out(button_7_out));
  Button button_8 (.out(button_8_out));
  Button button_9 (.out(button_9_out));
  Button button_10 (.out(button_10_out));
  Button button_11 (.out(button_11_out));
  Button button_12 (.out(button_12_out));
  Button button_13 (.out(button_13_out));
  Button button_14 (.out(button_14_out));
  Button button_15 (.out(button_15_out));
  Button button_16 (.out(button_16_out));

  // Notes on the sheet:
  //   Error
  //   +
  //   -
  //   X
  //   1
  //   4
  //   7
  //   C
  //   2
  //   3
  //   5
  //   6
  //   8
  //   9
  //   0
  //   B
  //   +
  //   -
  //   x
  //   =
endmodule

module lastestInput (
  input  in_1,
  input  in_2,
  input  in_3,
  input  in_4,
  input  in_5,
  input  in_6,
  input  in_7,
  input  in_8,
  input  in_9,
  input  in_10,
  input  in_11,
  input  in_12,
  input  in_13,
  input  in_14,
  output out_15,
  output out_16,
  output out_17,
  output out_18,
  output out_19,
  output out_20,
  output out_21,
  output out_22,
  output out_23,
  output out_24,
  output out_25,
  output out_26,
  output out_27,
  output out_28
);

  wire and_1_out, and_2_out, and_3_out, and_4_out, and_5_out, and_6_out, and_7_out, and_8_out, and_9_out,
       and_10_out, and_11_out, and_12_out, and_13_out, and_14_out, clock_1_out, nor_1_out, or_1_out,
       or_2_out, or_3_out, or_4_out, or_5_out, or_6_out, or_7_out, or_8_out, or_9_out, or_10_out, or_11_out,
       or_12_out, or_13_out, or_14_out, undriven;

  nor nor_1 (nor_1_out, in_14, in_13, in_12, in_11, in_1, in_2, in_3, in_4, in_5, in_6, in_7, in_8, in_9, in_10);
  and and_1 (and_1_out, out_15, nor_1_out);
  or or_1 (or_1_out, and_1_out, in_1);
  and and_2 (and_2_out, nor_1_out, out_16);
  or or_2 (or_2_out, and_2_out, in_2);
  and and_3 (and_3_out, out_17, nor_1_out);
  or or_3 (or_3_out, and_3_out, in_3);
  and and_4 (and_4_out, out_18, nor_1_out);
  or or_4 (or_4_out, and_4_out, in_4);
  and and_5 (and_5_out, out_19, nor_1_out);
  or or_5 (or_5_out, and_5_out, in_5);
  and and_6 (and_6_out, out_20, nor_1_out);
  or or_6 (or_6_out, and_6_out, in_6);
  and and_7 (and_7_out, out_21, nor_1_out);
  or or_7 (or_7_out, and_7_out, in_7);
  and and_8 (and_8_out, out_22, nor_1_out);
  or or_8 (or_8_out, and_8_out, in_8);
  and and_9 (and_9_out, out_23, nor_1_out);
  or or_9 (or_9_out, and_9_out, in_9);
  and and_10 (and_10_out, out_24, nor_1_out);
  or or_10 (or_10_out, and_10_out, in_10);
  and and_11 (and_11_out, out_25, nor_1_out);
  or or_11 (or_11_out, and_11_out, in_11);
  and and_12 (and_12_out, out_26, nor_1_out);
  or or_12 (or_12_out, and_12_out, in_12);
  and and_13 (and_13_out, out_27, nor_1_out);
  or or_13 (or_13_out, and_13_out, in_13);
  and and_14 (and_14_out, out_28, nor_1_out);
  or or_14 (or_14_out, and_14_out, in_14);
  D_Flip_Flop d_ff_1 (.D(or_1_out), .clk(clock_1_out), .Q(out_15));  // open: Qn, preset, reset
  D_Flip_Flop d_ff_2 (.D(or_2_out), .clk(clock_1_out), .Q(out_16), .reset(undriven));  // open: Qn, preset
  D_Flip_Flop d_ff_3 (.D(or_3_out), .clk(clock_1_out), .Q(out_17));  // open: Qn, preset, reset
  D_Flip_Flop d_ff_4 (.D(or_4_out), .clk(clock_1_out), .Q(out_18));  // open: Qn, preset, reset
  D_Flip_Flop d_ff_5 (.D(or_5_out), .clk(clock_1_out), .Q(out_19));  // open: Qn, preset, reset
  D_Flip_Flop d_ff_6 (.D(or_6_out), .clk(clock_1_out), .Q(out_20));  // open: Qn, preset, reset
  D_Flip_Flop d_ff_7 (.D(or_7_out), .clk(clock_1_out), .Q(out_21));  // open: Qn, preset, reset
  D_Flip_Flop d_ff_8 (.D(or_8_out), .clk(clock_1_out), .Q(out_22));  // open: Qn, preset, reset
  D_Flip_Flop d_ff_9 (.D(or_9_out), .clk(clock_1_out), .Q(out_23));  // open: Qn, preset, reset
  D_Flip_Flop d_ff_10 (.D(or_10_out), .clk(clock_1_out), .Q(out_24));  // open: Qn, preset, reset
  D_Flip_Flop d_ff_11 (.D(or_11_out), .clk(clock_1_out), .Q(out_25));  // open: Qn, preset, reset
  D_Flip_Flop d_ff_12 (.D(or_12_out), .clk(clock_1_out), .Q(out_26));  // open: Qn, preset, reset
  D_Flip_Flop d_ff_13 (.D(or_13_out), .clk(clock_1_out), .Q(out_27));  // open: Qn, preset, reset
  D_Flip_Flop d_ff_14 (.D(or_14_out), .clk(clock_1_out), .Q(out_28));  // open: Qn, preset, reset
  Clock clock_1 (.out(clock_1_out));
endmodule

module draft (
  input  in_1,
  input  in_2,
  input  in_3,
  input  in_4,
  input  in_5,
  input  in_6,
  input  in_7,
  input  in_8,
  input  in_9,
  input  in_10,
  input  in_11,
  input  in_12,
  output [3:0] out_13,
  output zero,
  output C,
  output N,
  output B
);

  wire risingdetector_1_out_2, risingdetector_2_out_2, risingdetector_3_out_2, risingdetector_4_out_2,
       risingdetector_7_out_2, risingdetector_8_out_2, risingdetector_9_out_2, risingdetector_10_out_2,
       risingdetector_11_out_2;

  RisingDetector risingdetector_1 (.in_1(in_6), .out_2(risingdetector_1_out_2));
  RisingDetector risingdetector_2 (.in_1(in_7), .out_2(risingdetector_2_out_2));
  RisingDetector risingdetector_3 (.in_1(in_8), .out_2(risingdetector_3_out_2));
  RisingDetector risingdetector_4 (.in_1(in_9), .out_2(risingdetector_4_out_2));
  RisingDetector risingdetector_5 (.in_1(in_10), .out_2(C));
  RisingDetector risingdetector_6 (.in_1(in_11), .out_2(zero));
  RisingDetector risingdetector_7 (.in_1(in_1), .out_2(risingdetector_7_out_2));
  RisingDetector risingdetector_8 (.in_1(in_2), .out_2(risingdetector_8_out_2));
  RisingDetector risingdetector_9 (.in_1(in_3), .out_2(risingdetector_9_out_2));
  RisingDetector risingdetector_10 (.in_1(in_4), .out_2(risingdetector_10_out_2));
  RisingDetector risingdetector_11 (.in_1(in_5), .out_2(risingdetector_11_out_2));
  RisingDetector risingdetector_12 (.in_1(in_12), .out_2(B));
  or or_1 (out_13[1], risingdetector_8_out_2, risingdetector_9_out_2, risingdetector_1_out_2, risingdetector_2_out_2, C, B);
  or or_2 (out_13[0], risingdetector_7_out_2, risingdetector_9_out_2, risingdetector_11_out_2, risingdetector_2_out_2, risingdetector_4_out_2, B);
  or or_3 (out_13[2], risingdetector_10_out_2, risingdetector_11_out_2, risingdetector_1_out_2, risingdetector_2_out_2);
  or or_4 (out_13[3], B, C, risingdetector_4_out_2, risingdetector_3_out_2);
  or or_5 (N, risingdetector_7_out_2, risingdetector_8_out_2, risingdetector_9_out_2, risingdetector_10_out_2, risingdetector_11_out_2, risingdetector_1_out_2, risingdetector_2_out_2, risingdetector_3_out_2, risingdetector_4_out_2, zero);
endmodule

module Draft2 (
  input  in_1,
  input  in_2,
  input  in_3,
  input  in_4,
  input  in_5,
  input  in_6,
  input  in_7,
  input  in_8,
  input  in_9,
  input  in_10,
  input  in_11,
  input  in_12,
  input  in_13,
  input  in_14,
  input  in_15,
  input  in_16,
  output [20:0] out_17,
  output C,
  output N,
  output Equa,
  output p,
  output m,
  output x,
  output load,
  output out_25,
  output out_26
);

  wire clock_1_out, d_ff_1_q, d_ff_2_q, draft_1_zero, or_3_out;
  wire [3:0] draft_1_out_13, lastestinputn_1_out_5, lastestinputn_1_out_6, lastestinputn_1_out_7,
       lastestinputn_1_out_8, lastestinputn_1_out_9, lastestinputn_1_out_10;
  wire [20:0] adder_1_out, adder_2_out, adder_3_out, adder_4_out, multi_1_c, multi_2_c, multi_3_c, multi_4_c,
       multi_5_c, multi_6_c;

  RisingDetector risingdetector_1 (.in_1(in_13), .out_2(p));
  RisingDetector risingdetector_2 (.in_1(in_14), .out_2(m));
  RisingDetector risingdetector_3 (.in_1(in_15), .out_2(x));
  RisingDetector risingdetector_4 (.in_1(in_16), .out_2(Equa));
  or or_1 (load, p, m, x);
  or or_2 (out_26, Equa, load);
  Hex_Digit_Display hex_digit_display_1 (.value(lastestinputn_1_out_10));  // open: dp
  draft draft_1 (
    .in_6(in_6), .in_7(in_7), .in_8(in_8), .in_9(in_9), .in_10(in_10), .in_11(in_11), .in_2(in_2),
    .in_3(in_3), .in_4(in_4), .in_5(in_5), .in_1(in_1), .in_12(in_12), .zero(draft_1_zero), .C(C),
    .out_13(draft_1_out_13), .N(N), .B(out_25));
  D_Flip_Flop d_ff_1 (.D(or_3_out), .clk(clock_1_out), .Q(d_ff_1_q));  // open: Qn, preset, reset
  or or_3 (or_3_out, C, load);
  Clock clock_1 (.out(clock_1_out));
  Hex_Digit_Display hex_digit_display_2 (.value(lastestinputn_1_out_9));  // open: dp
  Hex_Digit_Display hex_digit_display_3 (.value(lastestinputn_1_out_8));  // open: dp
  LED led_1 (.in(draft_1_zero));
  D_Flip_Flop d_ff_2 (.D(d_ff_1_q), .clk(clock_1_out), .Q(d_ff_2_q));  // open: Qn, preset, reset
  Hex_Digit_Display hex_digit_display_4 (.value(lastestinputn_1_out_7));  // open: dp
  Hex_Digit_Display hex_digit_display_5 (.value(lastestinputn_1_out_6));  // open: dp
  Hex_Digit_Display hex_digit_display_6 (.value(lastestinputn_1_out_5));  // open: dp
  lastestInputN lastestinputn_1 (
    .in_1({{17{1'b0}}, draft_1_out_13}), .C(d_ff_2_q), .N(N), .B(out_25), .out_5(lastestinputn_1_out_5),
    .out_6(lastestinputn_1_out_6), .out_7(lastestinputn_1_out_7), .out_8(lastestinputn_1_out_8),
    .out_9(lastestinputn_1_out_9), .out_10(lastestinputn_1_out_10));
  multi multi_1 (.B(21'h1), .A({{17{1'b0}}, lastestinputn_1_out_5}), .C(multi_1_c));  // open: Error
  multi multi_2 (.B(21'ha), .A({{17{1'b0}}, lastestinputn_1_out_6}), .C(multi_2_c));  // open: Error
  multi multi_3 (.B(21'h64), .A({{17{1'b0}}, lastestinputn_1_out_7}), .C(multi_3_c));  // open: Error
  multi multi_4 (.B(21'h3e8), .A({{17{1'b0}}, lastestinputn_1_out_8}), .C(multi_4_c));  // open: Error
  multi multi_5 (.B(21'h2710), .A({{17{1'b0}}, lastestinputn_1_out_9}), .C(multi_5_c));  // open: Error
  multi multi_6 (.B(21'h186a0), .A({{17{1'b0}}, lastestinputn_1_out_10}), .C(multi_6_c));  // open: Error
  Adder #(.width(21)) adder_1 (.a(multi_1_c), .b(multi_2_c), .out(adder_1_out));  // open: cin, cout
  Adder #(.width(21)) adder_2 (.a(adder_1_out), .b(multi_3_c), .out(adder_2_out));  // open: cin, cout
  Adder #(.width(21)) adder_3 (.a(adder_2_out), .b(multi_4_c), .out(adder_3_out));  // open: cin, cout
  Adder #(.width(21)) adder_4 (.a(adder_3_out), .b(multi_5_c), .out(adder_4_out));  // open: cin, cout
  Adder #(.width(21)) adder_5 (.a(adder_4_out), .b(multi_6_c), .out(out_17));  // open: cin, cout
endmodule

module FA (
  input  a,
  input  b,
  input  cin,
  output sum,
  output cout
);

  wire and_1_out, and_2_out, xor_1_out, xor_2_out;

  xor xor_1 (xor_1_out, a, b);
  and and_1 (and_1_out, a, b);
  xor xor_2 (xor_2_out, a, b);
  and and_2 (and_2_out, xor_2_out, cin);
  xor xor_3 (sum, xor_1_out, cin);
  or or_1 (cout, and_1_out, and_2_out);
endmodule

module plus (
  input  [20:0] in_1,
  input  [20:0] in_2,
  input  M,
  output overFlow,
  output [20:0] out_5
);

  wire fa_1_cout, fa_2_cout, fa_3_cout, fa_4_cout, fa_5_cout, fa_6_cout, fa_7_cout, fa_8_cout, fa_9_cout,
       fa_10_cout, fa_11_cout, fa_12_cout, fa_13_cout, fa_14_cout, fa_15_cout, fa_16_cout, fa_17_cout,
       fa_18_cout, fa_19_cout, fa_20_cout, fa_21_cout, xor_1_out, xor_2_out, xor_3_out, xor_4_out, xor_5_out,
       xor_6_out, xor_7_out, xor_8_out, xor_9_out, xor_10_out, xor_11_out, xor_12_out, xor_13_out,
       xor_14_out, xor_15_out, xor_16_out, xor_17_out, xor_18_out, xor_19_out, xor_20_out, xor_21_out;

  xor xor_1 (xor_1_out, M, in_2[0]);
  FA fa_1 (.a(in_1[0]), .b(xor_1_out), .cin(M), .sum(out_5[0]), .cout(fa_1_cout));
  xor xor_2 (xor_2_out, M, in_2[1]);
  FA fa_2 (.a(in_1[1]), .b(xor_2_out), .cin(fa_1_cout), .sum(out_5[1]), .cout(fa_2_cout));
  xor xor_3 (xor_3_out, M, in_2[2]);
  FA fa_3 (.a(in_1[2]), .b(xor_3_out), .cin(fa_2_cout), .sum(out_5[2]), .cout(fa_3_cout));
  xor xor_4 (xor_4_out, M, in_2[3]);
  FA fa_4 (.a(in_1[3]), .b(xor_4_out), .cin(fa_3_cout), .sum(out_5[3]), .cout(fa_4_cout));
  xor xor_5 (xor_5_out, M, in_2[4]);
  FA fa_5 (.a(in_1[4]), .b(xor_5_out), .cin(fa_4_cout), .sum(out_5[4]), .cout(fa_5_cout));
  xor xor_6 (xor_6_out, M, in_2[5]);
  FA fa_6 (.a(in_1[5]), .b(xor_6_out), .cin(fa_5_cout), .sum(out_5[5]), .cout(fa_6_cout));
  xor xor_7 (xor_7_out, M, in_2[6]);
  FA fa_7 (.a(in_1[6]), .b(xor_7_out), .cin(fa_6_cout), .sum(out_5[6]), .cout(fa_7_cout));
  xor xor_8 (xor_8_out, M, in_2[7]);
  FA fa_8 (.a(in_1[7]), .b(xor_8_out), .cin(fa_7_cout), .sum(out_5[7]), .cout(fa_8_cout));
  xor xor_9 (xor_9_out, M, in_2[8]);
  FA fa_9 (.a(in_1[8]), .b(xor_9_out), .cin(fa_8_cout), .sum(out_5[8]), .cout(fa_9_cout));
  xor xor_10 (xor_10_out, M, in_2[9]);
  FA fa_10 (.a(in_1[9]), .b(xor_10_out), .cin(fa_9_cout), .sum(out_5[9]), .cout(fa_10_cout));
  xor xor_11 (xor_11_out, M, in_2[10]);
  FA fa_11 (.a(in_1[10]), .b(xor_11_out), .cin(fa_10_cout), .sum(out_5[10]), .cout(fa_11_cout));
  xor xor_12 (xor_12_out, M, in_2[11]);
  FA fa_12 (.a(in_1[11]), .b(xor_12_out), .cin(fa_11_cout), .sum(out_5[11]), .cout(fa_12_cout));
  xor xor_13 (xor_13_out, M, in_2[12]);
  FA fa_13 (.a(in_1[12]), .b(xor_13_out), .cin(fa_12_cout), .sum(out_5[12]), .cout(fa_13_cout));
  xor xor_14 (xor_14_out, M, in_2[13]);
  FA fa_14 (.a(in_1[13]), .b(xor_14_out), .cin(fa_13_cout), .sum(out_5[13]), .cout(fa_14_cout));
  xor xor_15 (xor_15_out, M, in_2[14]);
  FA fa_15 (.a(in_1[14]), .b(xor_15_out), .cin(fa_14_cout), .sum(out_5[14]), .cout(fa_15_cout));
  xor xor_16 (xor_16_out, M, in_2[15]);
  FA fa_16 (.a(in_1[15]), .b(xor_16_out), .cin(fa_15_cout), .sum(out_5[15]), .cout(fa_16_cout));
  xor xor_17 (xor_17_out, M, in_2[16]);
  FA fa_17 (.a(in_1[16]), .b(xor_17_out), .cin(fa_16_cout), .sum(out_5[16]), .cout(fa_17_cout));
  xor xor_18 (xor_18_out, M, in_2[17]);
  FA fa_18 (.a(in_1[17]), .b(xor_18_out), .cin(fa_17_cout), .sum(out_5[17]), .cout(fa_18_cout));
  xor xor_19 (xor_19_out, M, in_2[18]);
  FA fa_19 (.a(in_1[18]), .b(xor_19_out), .cin(fa_18_cout), .sum(out_5[18]), .cout(fa_19_cout));
  xor xor_20 (xor_20_out, M, in_2[19]);
  FA fa_20 (.a(in_1[19]), .b(xor_20_out), .cin(fa_19_cout), .sum(out_5[19]), .cout(fa_20_cout));
  xor xor_21 (xor_21_out, M, in_2[20]);
  FA fa_21 (.a(in_1[20]), .b(xor_21_out), .cin(fa_20_cout), .sum(out_5[20]), .cout(fa_21_cout));
  xor xor_22 (overFlow, fa_21_cout, M);
endmodule

module RisingDetector (
  input  in_1,
  output out_2
);

  wire clock_1_out, d_ff_1_qn;

  D_Flip_Flop d_ff_1 (.D(in_1), .clk(clock_1_out), .Qn(d_ff_1_qn));  // open: Q, preset, reset
  Clock clock_1 (.out(clock_1_out));
  and and_1 (out_2, in_1, d_ff_1_qn);
endmodule

module shiftReg (
  input  SIN,
  input  [20:0] ParaIn,
  input  R,
  input  L,
  input  SL,
  input  SR,
  output [20:0] sreg
);

  wire clock_1_out;
  wire [4:1] and_1_out;
  wire [20:0] mux_1_b, shl_1_sreg_sl, shr_1_sreg_sr;

  SHR shr_1 (.sreg(sreg), .sin(SIN), .sreg_SR(shr_1_sreg_sr));
  SHL shl_1 (.sin(SIN), .sreg(sreg), .sreg_SL(shl_1_sreg_sl));
  and and_1 (and_1_out[1], ~R, L);  // AND_Gate
  mux mux_1 (
    .s({and_1_out, R}), .a4(sreg), .a3(shr_1_sreg_sr), .a2(shl_1_sreg_sl), .a1(ParaIn), .a0({21{1'b0}}),
    .b(mux_1_b));
  and and_2 (and_1_out[2], ~R, ~L, SL);  // AND_Gate
  and and_3 (and_1_out[3], ~R, ~L, ~SL, SR);  // AND_Gate
  Register #(.width(21)) register_1 (.D(mux_1_b), .clk(clock_1_out), .Q(sreg));  // open: en, clr
  Clock clock_1 (.out(clock_1_out));
  nor nor_1 (and_1_out[4], R, and_1_out[1], and_1_out[2], and_1_out[3]);
endmodule

module mux (
  input  [20:0] a4,
  input  [20:0] a3,
  input  [20:0] a2,
  input  [20:0] a1,
  input  [20:0] a0,
  input  [4:0] s,
  output [20:0] b
);

  wire [20:0] and_1_out, and_2_out, and_3_out, and_4_out, and_5_out, bit_extender_1_out, bit_extender_2_out,
       bit_extender_3_out, bit_extender_4_out, bit_extender_5_out;

  assign and_1_out = a4 & bit_extender_1_out;  // AND_Gate and_1, 21 bits wide
  assign bit_extender_1_out = {{20{s[4]}}, s[4]};  // Bit_Extender bit_extender_1
  assign and_2_out = a3 & bit_extender_2_out;  // AND_Gate and_2, 21 bits wide
  assign bit_extender_2_out = {{20{s[3]}}, s[3]};  // Bit_Extender bit_extender_2
  assign and_3_out = a2 & bit_extender_3_out;  // AND_Gate and_3, 21 bits wide
  assign bit_extender_3_out = {{20{s[2]}}, s[2]};  // Bit_Extender bit_extender_3
  assign and_4_out = a1 & bit_extender_4_out;  // AND_Gate and_4, 21 bits wide
  assign bit_extender_4_out = {{20{s[1]}}, s[1]};  // Bit_Extender bit_extender_4
  assign and_5_out = a0 & bit_extender_5_out;  // AND_Gate and_5, 21 bits wide
  assign bit_extender_5_out = {{20{s[0]}}, s[0]};  // Bit_Extender bit_extender_5
  assign b = and_1_out | and_2_out | and_3_out | and_4_out | and_5_out;  // OR_Gate or_1, 21 bits wide
endmodule

module SHR (
  input  [20:0] sreg,
  input  sin,
  output [20:0] sreg_SR
);


  assign sreg_SR = {sin, sreg[20:1]};
endmodule

module SHL (
  input  [20:0] sreg,
  input  sin,
  output [20:0] sreg_SL
);


  assign sreg_SL = {sreg[19:0], sin};
endmodule

module BCDunit (
  input  n,
  input  [2:0] c2c1c0,
  output [2:0] r2r1r0,
  output q
);

  wire and_1_out, and_3_out, and_4_out, not_1_out, not_2_out, not_3_out, or_1_out;
  wire [2:0] not_4_out;

  or or_1 (or_1_out, c2c1c0[0], n);
  and and_1 (and_1_out, c2c1c0[1], or_1_out);
  not not_1 (not_1_out, n);
  not not_2 (not_2_out, c2c1c0[1]);
  not not_3 (not_3_out, c2c1c0[0]);
  not not_4 (not_4_out[0], n);
  or or_2 (q, and_1_out, c2c1c0[2]);
  and and_2 (not_4_out[2], c2c1c0[2], n);
  and and_3 (and_3_out, n, c2c1c0[1], c2c1c0[0]);
  or or_3 (not_4_out[1], and_3_out, and_4_out);
  and and_4 (and_4_out, not_1_out, not_2_out, not_3_out);
  Multiplexer #(.width(3)) multiplexer_1 (.in0({c2c1c0[1:0], n}), .in1(not_4_out), .out(r2r1r0), .sel(q));
endmodule

module calculate (
  input  in_1,
  input  in_2,
  input  in_3,
  input  in_4,
  input  in_5,
  input  in_6,
  input  in_7,
  input  in_8,
  input  in_9,
  input  in_10,
  input  in_11,
  input  in_12,
  input  in_13,
  input  in_14,
  input  in_15,
  input  in_16,
  output P,
  output M,
  output MUL,
  output ERORR,
  output [3:0] out_21,
  output [3:0] out_22,
  output [3:0] out_23,
  output [3:0] out_24,
  output [3:0] out_25,
  output [3:0] out_26,
  output out_27
);

  wire AmA_out, AmN_out, and_1_out, and_2_out, and_3_out, and_4_out, and_5_out, and_6_out, and_7_out,
       and_8_out, and_9_out, and_10_out, and_11_out, and_12_out, and_13_out, and_14_out, and_15_out,
       and_17_out, and_18_out, and_19_out, and_20_out, and_21_out, and_22_out, and_23_out, and_24_out,
       and_25_out, and_26_out, and_27_out, and_28_out, ApA_out, ApN_out, AxA_out, AxN_out, clock_1_out,
       clock_2_out, clock_3_out, clock_4_out, clock_5_out, clock_6_out, clock_7_out, clock_8_out,
       clock_9_out, clock_10_out, clock_11_out, comparator_1_gt, comparator_2_gt, comparator_3_gt,
       comparator_4_lt, comparator_5_gt, comparator_5_lt, comparator_6_gt, comparator_6_lt, comparator_7_lt,
       comparator_8_lt, d_ff_1_q, d_ff_2_q, d_ff_3_q, d_ff_4_q, d_ff_5_q, d_ff_6_q, d_ff_7_q, draft2_1_c,
       draft2_1_equa, draft2_1_load, draft2_1_m, draft2_1_n, draft2_1_out_25, draft2_1_out_26, draft2_1_p,
       draft2_1_x, J_out, JIAN_out, lastestinput_1_out_15, lastestinput_1_out_16, lastestinput_3_out_15,
       lastestinput_3_out_20, lastestinput_3_out_24, newstate_1_a, newstate_1_am, newstate_1_amn,
       newstate_1_amnm, newstate_1_amnp, newstate_1_amnx, newstate_1_ap, newstate_1_apn, newstate_1_apnm,
       newstate_1_apnp, newstate_1_apnx, newstate_1_ax, newstate_1_axn, newstate_1_res, nor_1_out, not_1_out,
       not_2_out, not_3_out, or_1_out, or_2_out, or_3_out, or_4_out, or_5_out, or_6_out, or_7_out, or_8_out,
       or_9_out, or_10_out, or_11_out, or_12_out, or_13_out, or_14_out, or_15_out, or_16_out, or_17_out,
       or_18_out, or_19_out, or_20_out, or_21_out, plus_1_overflow, undriven, X_out;
  wire [4:0] formux_1_out_5, formux_2_out_5, formux_3_out_5, formux_4_out_5, formux_5_out_5, formux_6_out_5,
       formux_7_out_5, formux_8_out_5;
  wire [19:0] mux_1_b, register_1_q, register_4_q, tc_1_out_3, tc_2_out_3, tc_3_out_3, tc_4_out_3, tc_5_out_3;
  wire [20:0] draft2_1_out_17, multi_1_c, multi_2_c, mux_2_b, mux_3_b, mux_4_b, mux_5_b, mux_6_b, mux_7_b,
       mux_8_b, plus_1_out_5, plus_2_out_5, register_2_q, register_3_q, undriven_2;
  wire [20:20] register_1_q_2, register_4_q_2;

  _7_Segment_Display u_7_segment_display_1 (.g(out_27));  // open: f, a, b, e, d, c, dp
  TC tc_1 (.in_1(mux_1_b), .in_2(out_27), .out_3(tc_1_out_3));
  Hex_Digit_Display hex_digit_display_1 (.value(out_26));  // open: dp
  and and_1 (and_1_out, in_8, not_1_out);
  and and_2 (and_2_out, in_12, not_1_out);
  and and_3 (and_3_out, in_16, not_1_out);
  Hex_Digit_Display hex_digit_display_2 (.value(out_25));  // open: dp
  Hex_Digit_Display hex_digit_display_3 (.value(out_24));  // open: dp
  and and_4 (and_4_out, in_4, not_1_out);
  Hex_Digit_Display hex_digit_display_4 (.value(out_23));  // open: dp
  Hex_Digit_Display hex_digit_display_5 (.value(out_22));  // open: dp
  not not_1 (not_1_out, ERORR);
  not not_2 (not_2_out, lastestinput_1_out_16);
  BtoBCD btobcd_1 (.in_1(tc_1_out_3), .d0(out_21), .d1(out_22), .d2(out_23), .d3(out_24), .d4(out_25), .d5(out_26));
  Hex_Digit_Display hex_digit_display_6 (.value(out_21));  // open: dp
  and and_5 (and_5_out, in_2, not_1_out);
  and and_6 (and_6_out, in_3, not_1_out);
  and and_7 (and_7_out, in_1, not_1_out);
  and and_8 (and_8_out, in_6, not_1_out);
  and and_9 (and_9_out, in_7, not_1_out);
  and and_10 (and_10_out, in_5, not_1_out);
  and and_11 (and_11_out, in_10, not_1_out);
  and and_12 (and_12_out, in_11, not_1_out);
  and and_13 (and_13_out, in_9, not_1_out);
  and and_14 (and_14_out, in_15, not_1_out);
  and and_15 (and_15_out, in_13, not_2_out, not_1_out);
  not not_3 (not_3_out, nor_1_out);
  Draft2 draft2_1 (
    .in_1(and_5_out), .in_2(and_6_out), .in_3(and_7_out), .in_4(and_8_out), .in_5(and_9_out),
    .in_6(and_10_out), .in_7(and_11_out), .in_8(and_12_out), .in_9(and_13_out), .in_10(in_14),
    .in_11(and_14_out), .in_12(and_15_out), .in_13(and_4_out), .in_14(and_1_out), .in_15(and_2_out),
    .in_16(and_3_out), .out_17(draft2_1_out_17), .C(draft2_1_c), .N(draft2_1_n), .Equa(draft2_1_equa),
    .p(draft2_1_p), .m(draft2_1_m), .x(draft2_1_x), .load(draft2_1_load), .out_25(draft2_1_out_25),
    .out_26(draft2_1_out_26));
  lastestInput lastestinput_1 (
    .in_1(not_3_out), .in_2(draft2_1_out_26), .in_3(undriven), .in_7(draft2_1_equa),
    .out_15(lastestinput_1_out_15), .out_16(lastestinput_1_out_16));  // open: in_4, in_5, in_6, in_8, in_9, in_10, in_11, in_12, in_13, in_14, out_17, out_18, out_19, out_20, out_21, out_22, out_23, out_24, out_25, out_26, out_27, out_28
  nor nor_1 (nor_1_out, draft2_1_c, draft2_1_n, draft2_1_out_25);
  mux mux_1 (
    .s(formux_1_out_5), .a3(draft2_1_out_17), .a2({register_1_q_2[20], register_1_q}), .b({out_27, mux_1_b}));  // open: a4, a1, a0
  forMux formux_1 (
    .in_1(lastestinput_1_out_15), .in_2(lastestinput_1_out_16), .out_5(formux_1_out_5));  // open: in_3, in_4
  // AND_Gate and_16 has open pins: in0=lastestinput_1_out_16, out=open
  lastestInput lastestinput_2 (
    .in_1(and_17_out), .in_13(in_14), .out_15(ERORR));  // open: in_2, in_3, in_4, in_5, in_6, in_7, in_8, in_9, in_10, in_11, in_12, in_14, out_16, out_17, out_18, out_19, out_20, out_21, out_22, out_23, out_24, out_25, out_26, out_27, out_28
  Comparator #(.mode("unsigned"), .width(20)) comparator_1 (
    .a(tc_1_out_3), .b(20'hf423f), .gt(comparator_1_gt));  // open: eq, lt
  or or_1 (or_1_out, comparator_1_gt, or_18_out, or_21_out);
  and and_17 (and_17_out, lastestinput_1_out_16, or_1_out);
  newstate newstate_1 (
    .multi(draft2_1_x), .equal(draft2_1_equa), .reset(draft2_1_c), .number(draft2_1_n), .plus(draft2_1_p),
    .minus(draft2_1_m), .res(newstate_1_res), .A(newstate_1_a), .Am(newstate_1_am), .Ax(newstate_1_ax),
    .Ap(newstate_1_ap), .ApN(newstate_1_apn), .AmN(newstate_1_amn), .AxN(newstate_1_axn),
    .ApNp(newstate_1_apnp), .ApNx(newstate_1_apnx), .ApNm(newstate_1_apnm), .AmNp(newstate_1_amnp),
    .AmNx(newstate_1_amnx), .AmNm(newstate_1_amnm));
  or or_2 (or_2_out, draft2_1_equa, draft2_1_p, draft2_1_m);
  or or_3 (or_3_out, newstate_1_amnx, newstate_1_apnm, newstate_1_amnm);
  or or_4 (or_4_out, or_3_out, or_5_out);
  or or_5 (or_5_out, newstate_1_apnx, newstate_1_apnp, newstate_1_apnp);
  or or_6 (or_6_out, newstate_1_ax, newstate_1_am, newstate_1_ap);
  and AmN (AmN_out, or_2_out, newstate_1_amn);
  and AmA (AmA_out, newstate_1_am, draft2_1_equa);
  and AxA (AxA_out, newstate_1_ax, draft2_1_equa);
  and ApA (ApA_out, newstate_1_ap, draft2_1_equa);
  and ApN (ApN_out, newstate_1_apn, or_2_out);
  and and_18 (and_18_out, newstate_1_res, draft2_1_n);
  and AxN (AxN_out, newstate_1_axn, or_7_out);
  or or_7 (or_7_out, draft2_1_x, or_2_out);
  or or_8 (or_8_out, AmN_out, AmA_out);
  and and_19 (and_19_out, draft2_1_n, or_6_out);
  and and_20 (and_20_out, draft2_1_n, or_4_out);
  or or_9 (or_9_out, AxN_out, AxA_out);
  or or_10 (or_10_out, ApA_out, ApN_out);
  or or_11 (or_11_out, newstate_1_apnp, newstate_1_amnp);
  and J (J_out, or_11_out, draft2_1_equa);
  lastestInput lastestinput_3 (
    .in_1(and_18_out), .in_2(draft2_1_load), .in_6(and_19_out), .in_10(and_20_out),
    .out_15(lastestinput_3_out_15), .out_20(lastestinput_3_out_20), .out_24(lastestinput_3_out_24));  // open: in_3, in_4, in_5, in_7, in_8, in_9, in_11, in_12, in_13, in_14, out_16, out_17, out_18, out_19, out_21, out_22, out_23, out_25, out_26, out_27, out_28
  or or_12 (or_12_out, newstate_1_amnm, newstate_1_apnm);
  and JIAN (JIAN_out, draft2_1_equa, or_12_out);
  or or_13 (or_13_out, J_out, JIAN_out, or_12_out);
  or or_14 (or_14_out, or_11_out, or_12_out);
  lastestInput lastestinput_4 (
    .in_1(in_13), .in_2(draft2_1_c), .in_3(draft2_1_equa), .in_5(draft2_1_p), .in_6(draft2_1_m),
    .in_7(draft2_1_x), .out_19(P), .out_20(M), .out_21(MUL));  // open: in_4, in_8, in_9, in_10, in_11, in_12, in_13, in_14, out_15, out_16, out_17, out_18, out_22, out_23, out_24, out_25, out_26, out_27, out_28
  or or_15 (or_15_out, newstate_1_apnx, newstate_1_amnx);
  and X (X_out, draft2_1_equa, or_15_out);
  and and_21 (and_21_out, or_15_out, draft2_1_n);
  D_Flip_Flop d_ff_1 (.D(and_21_out), .clk(clock_1_out), .Q(d_ff_1_q));  // open: Qn, preset, reset
  Clock clock_1 (.out(clock_1_out));
  D_Flip_Flop d_ff_2 (.D(d_ff_1_q), .clk(clock_2_out), .Q(d_ff_2_q));  // open: Qn, preset, reset
  Clock clock_2 (.out(clock_2_out));
  or or_16 (or_16_out, X_out, d_ff_2_q);
  and and_22 (and_22_out, or_14_out, draft2_1_n);
  D_Flip_Flop d_ff_3 (.D(P), .clk(clock_3_out), .Q(d_ff_3_q));  // open: Qn, preset, reset
  Clock clock_3 (.out(clock_3_out));
  D_Flip_Flop d_ff_4 (.D(M), .clk(clock_4_out), .Q(d_ff_4_q));  // open: Qn, preset, reset
  Clock clock_4 (.out(clock_4_out));
  D_Flip_Flop d_ff_5 (.D(MUL), .clk(clock_5_out), .Q(d_ff_5_q));  // open: Qn, preset, reset
  Clock clock_5 (.out(clock_5_out));
  LED led_1 (.in(newstate_1_a));
  LED led_2 (.in(newstate_1_ax));
  LED led_3 (.in(newstate_1_ap));
  LED led_4 (.in(newstate_1_apn));
  LED led_5 (.in(newstate_1_axn));
  LED led_6 (.in(newstate_1_amn));
  LED led_7 (.in(newstate_1_amnx));
  LED led_8 (.in(newstate_1_apnm));
  LED led_9 (.in(newstate_1_amnm));
  LED led_10 (.in(newstate_1_apnx));
  LED led_11 (.in(newstate_1_apnp));
  LED led_12 (.in(newstate_1_amnp));
  LED led_13 (.in(newstate_1_am));
  forMux formux_2 (.in_1(or_17_out), .out_5(formux_2_out_5));  // open: in_2, in_3, in_4
  or or_17 (or_17_out, ApA_out, AmA_out);
  forMux formux_3 (.out_5(formux_3_out_5));  // open: in_1, in_2, in_3, in_4
  mux mux_2 (
    .s(formux_2_out_5), .a4(register_2_q), .a3({register_1_q_2[20], register_1_q}), .b(mux_2_b));  // open: a2, a1, a0
  mux mux_3 (.s(formux_3_out_5), .a4(register_2_q), .a3(undriven_2), .b(mux_3_b));  // open: a2, a1, a0
  mux mux_4 (
    .s(formux_4_out_5), .a4(register_2_q), .a3({register_1_q_2[20], register_1_q}), .b(mux_4_b));  // open: a2, a1, a0
  forMux formux_4 (.in_1(AxA_out), .out_5(formux_4_out_5));  // open: in_2, in_3, in_4
  or or_18 (or_18_out, comparator_2_gt, comparator_3_gt);
  mux mux_5 (.s(formux_5_out_5), .a4(register_2_q), .a3(register_3_q), .b(mux_5_b));  // open: a2, a1, a0
  forMux formux_5 (.in_1(d_ff_2_q), .out_5(formux_5_out_5));  // open: in_2, in_3, in_4
  multi multi_1 (.B(mux_4_b), .A({register_1_q_2[20], register_1_q}), .C(multi_1_c));  // open: Error
  multi multi_2 (.B(mux_5_b), .A(register_2_q), .C(multi_2_c));  // open: Error
  plus plus_1 (
    .in_1({register_1_q_2[20], register_1_q}), .in_2(mux_2_b), .M(or_8_out), .overFlow(plus_1_overflow),
    .out_5(plus_1_out_5));
  or or_19 (or_19_out, or_10_out, or_8_out, d_ff_6_q, d_ff_7_q);
  plus plus_2 (.in_1(register_2_q), .in_2(mux_3_b), .M(JIAN_out), .out_5(plus_2_out_5));  // open: overFlow
  Register #(.width(21)) register_1 (
    .D(mux_6_b), .clk(clock_6_out), .Q({register_1_q_2[20], register_1_q}));  // open: en, clr
  mux mux_6 (
    .s(formux_6_out_5), .a4({register_1_q_2[20], register_1_q}), .a3(plus_1_out_5), .a2(multi_1_c),
    .a1({21{1'b0}}), .a0(draft2_1_out_17), .b(mux_6_b));
  Clock clock_6 (.out(clock_6_out));
  forMux formux_6 (
    .in_1(or_19_out), .in_2(or_20_out), .in_4(lastestinput_3_out_15), .out_5(formux_6_out_5));  // open: in_3
  buf or_20 (or_20_out, or_9_out);  // OR_Gate
  D_Flip_Flop d_ff_6 (.D(or_13_out), .clk(clock_7_out), .Q(d_ff_6_q));  // open: Qn, preset, reset
  Clock clock_7 (.out(clock_7_out));
  Register #(.width(21)) register_2 (.D(mux_7_b), .clk(clock_8_out), .Q(register_2_q));  // open: en, clr
  mux mux_7 (
    .s(formux_7_out_5), .a4(register_2_q), .a3(plus_2_out_5), .a2(multi_2_c), .a1(register_3_q),
    .a0(draft2_1_out_17), .b(mux_7_b));
  Clock clock_8 (.out(clock_8_out));
  forMux formux_7 (
    .in_1(or_13_out), .in_2(or_16_out), .in_3(and_22_out), .in_4(lastestinput_3_out_20),
    .out_5(formux_7_out_5));
  mux mux_8 (.s(formux_8_out_5), .a4(register_3_q), .a0(draft2_1_out_17), .b(mux_8_b));  // open: a3, a2, a1
  forMux formux_8 (.in_4(lastestinput_3_out_24), .out_5(formux_8_out_5));  // open: in_1, in_2, in_3
  Register #(.width(21)) register_3 (.D(mux_8_b), .clk(clock_9_out), .Q(register_3_q));  // open: en, clr
  Clock clock_9 (.out(clock_9_out));
  Clock clock_10 (.out(clock_10_out));
  Comparator #(.mode("unsigned"), .width(20)) comparator_2 (
    .a(tc_4_out_3), .b(20'hf423f), .gt(comparator_2_gt));  // open: eq, lt
  D_Flip_Flop d_ff_7 (.D(X_out), .clk(clock_10_out), .Q(d_ff_7_q));  // open: Qn, preset, reset
  Comparator #(.mode("unsigned"), .width(20)) comparator_3 (
    .a(tc_2_out_3), .b(20'hf423f), .gt(comparator_3_gt));  // open: eq, lt
  TC tc_2 (.in_1(register_1_q), .in_2(register_1_q_2[20]), .out_3(tc_2_out_3));
  TC tc_3 (.in_1(register_4_q), .in_2(register_4_q_2[20]), .out_3(tc_3_out_3));
  TC tc_4 (.in_1(register_2_q[19:0]), .in_2(register_2_q[20]), .out_3(tc_4_out_3));
  Register #(.width(21)) register_4 (
    .D({register_1_q_2[20], register_1_q}), .clk(clock_11_out), .Q({register_4_q_2[20], register_4_q}));  // open: en, clr
  Clock clock_11 (.out(clock_11_out));
  Comparator #(.mode("unsigned"), .width(20)) comparator_4 (
    .a(tc_2_out_3), .b(tc_3_out_3), .lt(comparator_4_lt));  // open: gt, eq
  and and_23 (and_23_out, d_ff_5_q, comparator_4_lt);
  or or_21 (or_21_out, and_23_out, and_25_out, and_24_out);
  and and_24 (and_24_out, comparator_7_lt, and_26_out);
  TC tc_5 (.in_1(mux_2_b[19:0]), .in_2(mux_2_b[20]), .out_3(tc_5_out_3));
  Comparator #(.width(21)) comparator_5 (
    .a(mux_2_b), .b({21{1'b0}}), .gt(comparator_5_gt), .lt(comparator_5_lt));  // open: eq
  Comparator #(.width(21)) comparator_6 (
    .a({register_4_q_2[20], register_4_q}), .b({21{1'b0}}), .gt(comparator_6_gt), .lt(comparator_6_lt));  // open: eq
  Comparator #(.mode("unsigned"), .width(20)) comparator_7 (
    .a(tc_2_out_3), .b(tc_5_out_3), .lt(comparator_7_lt));  // open: gt, eq
  and and_25 (and_25_out, and_28_out, comparator_8_lt);
  and and_26 (and_26_out, d_ff_3_q, and_27_out);
  and and_27 (and_27_out, comparator_5_gt, comparator_6_gt);
  and and_28 (and_28_out, comparator_6_lt, d_ff_4_q);
  Comparator #(.width(21)) comparator_8 (
    .a({register_4_q_2[20], register_4_q}), .b({register_1_q_2[20], register_1_q}), .lt(comparator_8_lt));  // open: gt, eq

  // Notes on the sheet:
  //   A
  //   Ax
  //   A-
  //   A+
  //   A+N
  //   AxN
  //   A-N
  //   A-Nx
  //   A+N-
  //   A-N-
  //   A+Nx
  //   A+N+
  //   A-N+
endmodule

module BCD (
  input  [5:0] in_1,
  output [3:0] weight0,
  output [3:0] weight1
);

  wire [2:0] bcdunit_1_r2r1r0, bcdunit_2_r2r1r0, bcdunit_3_r2r1r0, bcdunit_4_r2r1r0;
  wire [2:2] bcdunit_4_q;

  BCDunit bcdunit_1 (.n(in_1[3]), .c2c1c0({1'b0, in_1[5:4]}), .r2r1r0(bcdunit_1_r2r1r0), .q(weight1[2]));
  BCDunit bcdunit_2 (.n(in_1[2]), .c2c1c0(bcdunit_1_r2r1r0), .r2r1r0(bcdunit_2_r2r1r0), .q(weight1[1]));
  BCDunit bcdunit_3 (.n(in_1[1]), .c2c1c0(bcdunit_2_r2r1r0), .r2r1r0(bcdunit_3_r2r1r0), .q(weight1[0]));
  BCDunit bcdunit_4 (.n(in_1[0]), .c2c1c0(bcdunit_3_r2r1r0), .r2r1r0(bcdunit_4_r2r1r0), .q(bcdunit_4_q[2]));
  Adder #(.width(4)) adder_1 (
    .a({1'b0, bcdunit_4_r2r1r0}), .b({1'b0, bcdunit_4_q[2], 1'b0, bcdunit_4_q[2]}), .out(weight0));  // open: cin, cout

  assign weight1[3] = 1'b0;
endmodule

module pp (
  input  in_1,
  input  in_2,
  input  in_3,
  input  in_4,
  output [3:0] out_5
);

  wire adder_1_cout, adder_2_cout;

  Adder #(.width(1)) adder_1 (.a(in_1), .b(in_4), .out(out_5[0]), .cin(1'b0), .cout(adder_1_cout));
  Adder #(.width(1)) adder_2 (.a(in_2), .b(1'b0), .out(out_5[1]), .cin(adder_1_cout), .cout(adder_2_cout));
  Adder #(.width(1)) adder_3 (.a(in_4), .b(in_3), .out(out_5[2]), .cin(adder_2_cout), .cout(out_5[3]));
endmodule
module multi (
  input  [20:0] A,
  input  [20:0] B,
  output [20:0] C,
  output Error
);

  wire and_2_out, and_3_out, and_4_out, and_5_out, and_6_out, and_7_out, and_8_out, and_9_out, and_10_out,
       and_11_out, and_12_out, and_13_out, and_14_out, and_15_out, and_16_out, and_17_out, and_18_out,
       and_19_out, and_20_out, and_21_out, and_22_out, and_23_out, and_24_out, and_25_out, and_26_out,
       and_27_out, and_28_out, and_29_out, and_30_out, and_31_out, and_32_out, and_33_out, and_34_out,
       and_35_out, and_36_out, and_37_out, and_38_out, and_39_out, and_40_out, and_41_out, and_42_out,
       and_43_out, and_44_out, and_45_out, and_46_out, and_47_out, and_48_out, and_49_out, and_50_out,
       and_51_out, and_52_out, and_53_out, and_54_out, and_55_out, and_56_out, and_57_out, and_58_out,
       and_59_out, and_60_out, and_61_out, and_62_out, and_63_out, and_64_out, and_65_out, and_66_out,
       and_67_out, and_68_out, and_69_out, and_70_out, and_71_out, and_72_out, and_73_out, and_74_out,
       and_75_out, and_76_out, and_77_out, and_78_out, and_79_out, and_80_out, and_81_out, and_82_out,
       and_83_out, and_84_out, and_85_out, and_86_out, and_87_out, and_88_out, and_89_out, and_90_out,
       and_91_out, and_92_out, and_93_out, and_94_out, and_95_out, and_96_out, and_97_out, and_98_out,
       and_99_out, and_100_out, and_101_out, and_102_out, and_103_out, and_104_out, and_105_out, and_106_out,
       and_107_out, and_108_out, and_109_out, and_110_out, and_111_out, and_112_out, and_113_out,
       and_114_out, and_115_out, and_116_out, and_117_out, and_118_out, and_119_out, and_120_out,
       and_121_out, and_122_out, and_123_out, and_124_out, and_125_out, and_126_out, and_127_out,
       and_128_out, and_129_out, and_130_out, and_131_out, and_132_out, and_133_out, and_134_out,
       and_135_out, and_136_out, and_137_out, and_138_out, and_139_out, and_140_out, and_141_out,
       and_142_out, and_143_out, and_144_out, and_145_out, and_146_out, and_147_out, and_148_out,
       and_149_out, and_150_out, and_151_out, and_152_out, and_153_out, and_154_out, and_155_out,
       and_156_out, and_157_out, and_158_out, and_159_out, and_160_out, and_161_out, and_162_out,
       and_163_out, and_164_out, and_165_out, and_166_out, and_167_out, and_168_out, and_169_out,
       and_170_out, and_171_out, and_172_out, and_173_out, and_174_out, and_175_out, and_176_out,
       and_177_out, and_178_out, and_179_out, and_180_out, and_181_out, and_182_out, and_183_out,
       and_184_out, and_185_out, and_186_out, and_187_out, and_188_out, and_189_out, and_190_out,
       and_191_out, and_192_out, and_193_out, and_194_out, and_195_out, and_196_out, and_197_out,
       and_198_out, and_199_out, and_200_out, and_201_out, and_202_out, and_203_out, and_204_out,
       and_205_out, and_206_out, and_207_out, and_208_out, and_209_out, and_210_out, and_211_out,
       and_212_out, and_213_out, and_214_out, and_215_out, and_216_out, and_217_out, and_218_out,
       and_219_out, and_220_out, and_221_out, and_222_out, and_223_out, and_224_out, and_225_out,
       and_226_out, and_227_out, and_228_out, and_229_out, and_230_out, and_231_out, and_232_out,
       and_233_out, and_234_out, and_235_out, and_236_out, and_237_out, and_238_out, and_239_out,
       and_240_out, and_241_out, and_242_out, and_243_out, and_244_out, and_245_out, and_246_out,
       and_247_out, and_248_out, and_249_out, and_250_out, and_251_out, and_252_out, and_253_out,
       and_254_out, and_255_out, and_256_out, and_257_out, and_258_out, and_259_out, and_260_out,
       and_261_out, and_262_out, and_263_out, and_264_out, and_265_out, and_266_out, and_267_out,
       and_268_out, and_269_out, and_270_out, and_271_out, and_272_out, and_273_out, and_274_out,
       and_275_out, and_276_out, and_277_out, and_278_out, and_279_out, and_280_out, and_281_out,
       and_282_out, and_283_out, and_284_out, and_285_out, and_286_out, and_287_out, and_288_out,
       and_289_out, and_290_out, and_291_out, and_292_out, and_293_out, and_294_out, and_295_out,
       and_296_out, and_297_out, and_298_out, and_299_out, and_300_out, and_301_out, and_302_out,
       and_303_out, and_304_out, and_305_out, and_306_out, and_307_out, and_308_out, and_309_out,
       and_310_out, and_311_out, and_312_out, and_313_out, and_314_out, and_315_out, and_316_out,
       and_317_out, and_318_out, and_319_out, and_320_out, and_321_out, and_322_out, and_323_out,
       and_324_out, and_325_out, and_326_out, and_327_out, and_328_out, and_329_out, and_330_out,
       and_331_out, and_332_out, and_333_out, and_334_out, and_335_out, and_336_out, and_337_out,
       and_338_out, and_339_out, and_340_out, and_341_out, and_342_out, and_343_out, and_344_out,
       and_345_out, and_346_out, and_347_out, and_348_out, and_349_out, and_350_out, and_351_out,
       and_352_out, and_353_out, and_354_out, and_355_out, and_356_out, and_357_out, and_358_out,
       and_359_out, and_360_out, and_361_out, and_362_out, and_363_out, and_364_out, and_365_out,
       and_366_out, and_367_out, and_368_out, and_369_out, and_370_out, and_371_out, and_372_out,
       and_373_out, and_374_out, and_375_out, and_376_out, and_377_out, and_378_out, and_379_out,
       and_380_out, and_381_out, and_382_out, and_383_out, and_384_out, and_385_out, and_386_out,
       and_387_out, and_388_out, and_389_out, and_390_out, and_391_out, and_392_out, and_393_out,
       and_394_out, and_395_out, and_396_out, and_397_out, and_398_out, and_399_out, and_400_out, fa_1_cout,
       fa_2_cout, fa_2_sum, fa_3_cout, fa_4_cout, fa_4_sum, fa_5_cout, fa_5_sum, fa_6_cout, fa_7_cout,
       fa_7_sum, fa_8_cout, fa_8_sum, fa_9_cout, fa_9_sum, fa_10_cout, fa_11_cout, fa_11_sum, fa_12_cout,
       fa_12_sum, fa_13_cout, fa_13_sum, fa_14_cout, fa_14_sum, fa_15_cout, fa_16_cout, fa_16_sum,
       fa_17_cout, fa_17_sum, fa_18_cout, fa_18_sum, fa_19_cout, fa_19_sum, fa_20_cout, fa_20_sum,
       fa_21_cout, fa_22_cout, fa_22_sum, fa_23_cout, fa_23_sum, fa_24_cout, fa_24_sum, fa_25_cout,
       fa_25_sum, fa_26_cout, fa_26_sum, fa_27_cout, fa_27_sum, fa_28_cout, fa_29_cout, fa_29_sum,
       fa_30_cout, fa_30_sum, fa_31_cout, fa_31_sum, fa_32_cout, fa_32_sum, fa_33_cout, fa_33_sum,
       fa_34_cout, fa_34_sum, fa_35_cout, fa_35_sum, fa_36_cout, fa_37_cout, fa_37_sum, fa_38_cout,
       fa_38_sum, fa_39_cout, fa_39_sum, fa_40_cout, fa_40_sum, fa_41_cout, fa_41_sum, fa_42_cout, fa_42_sum,
       fa_43_cout, fa_43_sum, fa_44_cout, fa_44_sum, fa_45_cout, fa_46_cout, fa_46_sum, fa_47_cout,
       fa_47_sum, fa_48_cout, fa_48_sum, fa_49_cout, fa_49_sum, fa_50_cout, fa_50_sum, fa_51_cout, fa_51_sum,
       fa_52_cout, fa_52_sum, fa_53_cout, fa_53_sum, fa_54_cout, fa_54_sum, fa_55_cout, fa_56_cout,
       fa_56_sum, fa_57_cout, fa_57_sum, fa_58_cout, fa_58_sum, fa_59_cout, fa_59_sum, fa_60_cout, fa_60_sum,
       fa_61_cout, fa_61_sum, fa_62_cout, fa_62_sum, fa_63_cout, fa_63_sum, fa_64_cout, fa_64_sum,
       fa_65_cout, fa_65_sum, fa_66_cout, fa_67_cout, fa_67_sum, fa_68_cout, fa_68_sum, fa_69_cout,
       fa_69_sum, fa_70_cout, fa_70_sum, fa_71_cout, fa_71_sum, fa_72_cout, fa_72_sum, fa_73_cout, fa_73_sum,
       fa_74_cout, fa_74_sum, fa_75_cout, fa_75_sum, fa_76_cout, fa_76_sum, fa_77_cout, fa_77_sum,
       fa_78_cout, fa_79_cout, fa_79_sum, fa_80_cout, fa_80_sum, fa_81_cout, fa_81_sum, fa_82_cout,
       fa_82_sum, fa_83_cout, fa_83_sum, fa_84_cout, fa_84_sum, fa_85_cout, fa_85_sum, fa_86_cout, fa_86_sum,
       fa_87_cout, fa_87_sum, fa_88_cout, fa_88_sum, fa_89_cout, fa_89_sum, fa_90_cout, fa_90_sum,
       fa_91_cout, fa_92_cout, fa_92_sum, fa_93_cout, fa_93_sum, fa_94_cout, fa_94_sum, fa_95_cout,
       fa_95_sum, fa_96_cout, fa_96_sum, fa_97_cout, fa_97_sum, fa_98_cout, fa_98_sum, fa_99_cout, fa_99_sum,
       fa_100_cout, fa_100_sum, fa_101_cout, fa_101_sum, fa_102_cout, fa_102_sum, fa_103_cout, fa_103_sum,
       fa_104_cout, fa_104_sum, fa_105_cout, fa_106_cout, fa_106_sum, fa_107_cout, fa_107_sum, fa_108_cout,
       fa_108_sum, fa_109_cout, fa_109_sum, fa_110_cout, fa_110_sum, fa_111_cout, fa_111_sum, fa_112_cout,
       fa_112_sum, fa_113_cout, fa_113_sum, fa_114_cout, fa_114_sum, fa_115_cout, fa_115_sum, fa_116_cout,
       fa_116_sum, fa_117_cout, fa_117_sum, fa_118_cout, fa_118_sum, fa_119_cout, fa_119_sum, fa_120_cout,
       fa_121_cout, fa_121_sum, fa_122_cout, fa_122_sum, fa_123_cout, fa_123_sum, fa_124_cout, fa_124_sum,
       fa_125_cout, fa_125_sum, fa_126_cout, fa_126_sum, fa_127_cout, fa_127_sum, fa_128_cout, fa_128_sum,
       fa_129_cout, fa_129_sum, fa_130_cout, fa_130_sum, fa_131_cout, fa_131_sum, fa_132_cout, fa_132_sum,
       fa_133_cout, fa_133_sum, fa_134_cout, fa_134_sum, fa_135_cout, fa_135_sum, fa_136_cout, fa_137_cout,
       fa_137_sum, fa_138_cout, fa_138_sum, fa_139_cout, fa_139_sum, fa_140_cout, fa_140_sum, fa_141_cout,
       fa_141_sum, fa_142_cout, fa_142_sum, fa_143_cout, fa_143_sum, fa_144_cout, fa_144_sum, fa_145_cout,
       fa_145_sum, fa_146_cout, fa_146_sum, fa_147_cout, fa_147_sum, fa_148_cout, fa_148_sum, fa_149_cout,
       fa_149_sum, fa_150_cout, fa_150_sum, fa_151_cout, fa_151_sum, fa_152_cout, fa_152_sum, fa_153_cout,
       fa_154_cout, fa_154_sum, fa_155_cout, fa_155_sum, fa_156_cout, fa_156_sum, fa_157_cout, fa_157_sum,
       fa_158_cout, fa_158_sum, fa_159_cout, fa_159_sum, fa_160_cout, fa_160_sum, fa_161_cout, fa_161_sum,
       fa_162_cout, fa_162_sum, fa_163_cout, fa_163_sum, fa_164_cout, fa_164_sum, fa_165_cout, fa_165_sum,
       fa_166_cout, fa_166_sum, fa_167_cout, fa_167_sum, fa_168_cout, fa_168_sum, fa_169_cout, fa_169_sum,
       fa_170_cout, fa_170_sum, fa_171_cout, fa_172_cout, fa_172_sum, fa_173_cout, fa_173_sum, fa_174_cout,
       fa_174_sum, fa_175_cout, fa_175_sum, fa_176_cout, fa_176_sum, fa_177_cout, fa_177_sum, fa_178_cout,
       fa_178_sum, fa_179_cout, fa_179_sum, fa_180_cout, fa_180_sum, fa_181_cout, fa_181_sum, fa_182_cout,
       fa_182_sum, fa_183_cout, fa_183_sum, fa_184_cout, fa_184_sum, fa_185_cout, fa_185_sum, fa_186_cout,
       fa_186_sum, fa_187_cout, fa_187_sum, fa_188_cout, fa_188_sum, fa_189_cout, fa_189_sum, fa_190_cout,
       fa_191_cout, fa_191_sum, fa_192_cout, fa_192_sum, fa_193_cout, fa_193_sum, fa_194_cout, fa_194_sum,
       fa_195_cout, fa_195_sum, fa_196_cout, fa_196_sum, fa_197_cout, fa_197_sum, fa_198_cout, fa_198_sum,
       fa_199_cout, fa_199_sum, fa_200_cout, fa_200_sum, fa_201_cout, fa_201_sum, fa_202_cout, fa_202_sum,
       fa_203_cout, fa_203_sum, fa_204_cout, fa_204_sum, fa_205_cout, fa_205_sum, fa_206_cout, fa_206_sum,
       fa_207_cout, fa_207_sum, fa_208_cout, fa_208_sum, fa_209_cout, fa_209_sum, fa_210_cout, fa_210_sum,
       fa_211_cout, fa_211_sum, fa_212_cout, fa_212_sum, fa_213_cout, fa_213_sum, fa_214_cout, fa_214_sum,
       fa_215_cout, fa_215_sum, fa_216_cout, fa_216_sum, fa_217_cout, fa_217_sum, fa_218_cout, fa_218_sum,
       fa_219_cout, fa_219_sum, fa_220_cout, fa_220_sum, fa_221_cout, fa_221_sum, fa_222_cout, fa_222_sum,
       fa_223_cout, fa_223_sum, fa_224_cout, fa_224_sum, fa_225_cout, fa_225_sum, fa_226_cout, fa_226_sum,
       fa_227_cout, fa_227_sum, fa_228_cout, fa_228_sum, fa_229_cout, fa_229_sum, fa_230_cout, fa_230_sum,
       fa_231_cout, fa_231_sum, fa_232_cout, fa_232_sum, fa_233_cout, fa_233_sum, fa_234_cout, fa_234_sum,
       fa_235_cout, fa_235_sum, fa_236_cout, fa_236_sum, fa_237_cout, fa_237_sum, fa_238_cout, fa_238_sum,
       fa_239_cout, fa_239_sum, fa_240_cout, fa_240_sum, fa_241_cout, fa_241_sum, fa_242_cout, fa_242_sum,
       fa_243_cout, fa_243_sum, fa_244_cout, fa_244_sum, fa_245_cout, fa_245_sum, fa_246_cout, fa_246_sum,
       fa_247_cout, fa_247_sum, fa_248_cout, fa_248_sum, fa_249_cout, fa_249_sum, fa_250_cout, fa_250_sum,
       fa_251_cout, fa_251_sum, fa_252_cout, fa_252_sum, fa_253_cout, fa_253_sum, fa_254_cout, fa_254_sum,
       fa_255_cout, fa_255_sum, fa_256_cout, fa_256_sum, fa_257_cout, fa_257_sum, fa_258_cout, fa_258_sum,
       fa_259_cout, fa_259_sum, fa_260_cout, fa_260_sum, fa_261_cout, fa_261_sum, fa_262_cout, fa_262_sum,
       fa_263_cout, fa_263_sum, fa_264_cout, fa_264_sum, fa_265_cout, fa_265_sum, fa_266_cout, fa_266_sum,
       fa_267_cout, fa_267_sum, fa_268_cout, fa_268_sum, fa_269_cout, fa_269_sum, fa_270_cout, fa_270_sum,
       fa_271_cout, fa_271_sum, fa_272_cout, fa_272_sum, fa_273_cout, fa_273_sum, fa_274_cout, fa_274_sum,
       fa_275_cout, fa_275_sum, fa_276_cout, fa_276_sum, fa_277_cout, fa_277_sum, fa_278_cout, fa_278_sum,
       fa_279_cout, fa_279_sum, fa_280_cout, fa_280_sum, fa_281_cout, fa_281_sum, fa_282_cout, fa_282_sum,
       fa_283_cout, fa_283_sum, fa_284_cout, fa_284_sum, fa_285_cout, fa_285_sum, fa_286_cout, fa_286_sum,
       fa_287_cout, fa_287_sum, fa_288_cout, fa_288_sum, fa_289_cout, fa_289_sum, fa_290_cout, fa_290_sum,
       fa_291_cout, fa_291_sum, fa_292_cout, fa_292_sum, fa_293_cout, fa_293_sum, fa_294_cout, fa_294_sum,
       fa_295_cout, fa_295_sum, fa_296_cout, fa_296_sum, fa_297_cout, fa_297_sum, fa_298_cout, fa_298_sum,
       fa_299_cout, fa_299_sum, fa_300_cout, fa_300_sum, fa_301_cout, fa_301_sum, fa_302_cout, fa_302_sum,
       fa_303_cout, fa_303_sum, fa_304_cout, fa_304_sum, fa_305_cout, fa_305_sum, fa_306_cout, fa_306_sum,
       fa_307_cout, fa_307_sum, fa_308_cout, fa_308_sum, fa_309_cout, fa_309_sum, fa_310_cout, fa_310_sum,
       fa_311_cout, fa_311_sum, fa_312_cout, fa_312_sum, fa_313_cout, fa_313_sum, fa_314_cout, fa_314_sum,
       fa_315_cout, fa_315_sum, fa_316_cout, fa_316_sum, fa_317_cout, fa_317_sum, fa_318_cout, fa_318_sum,
       fa_319_cout, fa_319_sum, fa_320_cout, fa_320_sum, fa_321_cout, fa_321_sum, fa_322_cout, fa_322_sum,
       fa_323_cout, fa_323_sum, fa_324_cout, fa_324_sum, fa_325_cout, fa_325_sum, fa_326_cout, fa_326_sum,
       fa_327_cout, fa_327_sum, fa_328_cout, fa_328_sum, fa_329_cout, fa_329_sum, fa_330_cout, fa_330_sum,
       fa_331_cout, fa_331_sum, fa_332_cout, fa_332_sum, fa_333_cout, fa_333_sum, fa_334_cout, fa_334_sum,
       fa_335_cout, fa_335_sum, fa_336_cout, fa_336_sum, fa_337_cout, fa_337_sum, fa_338_cout, fa_338_sum,
       fa_339_cout, fa_339_sum, fa_340_cout, fa_340_sum, fa_341_cout, fa_341_sum, fa_342_cout, fa_342_sum,
       fa_343_cout, fa_343_sum, fa_344_cout, fa_344_sum, fa_345_cout, fa_345_sum, fa_346_cout, fa_346_sum,
       fa_347_cout, fa_347_sum, fa_348_cout, fa_348_sum, fa_349_cout, fa_349_sum, fa_350_cout, fa_350_sum,
       fa_351_cout, fa_351_sum, fa_352_cout, fa_352_sum, fa_353_cout, fa_353_sum, fa_354_cout, fa_354_sum,
       fa_355_cout, fa_355_sum, fa_356_cout, fa_356_sum, fa_357_cout, fa_357_sum, fa_358_cout, fa_358_sum,
       fa_359_cout, fa_359_sum, fa_360_cout, fa_360_sum, fa_361_cout, fa_361_sum, fa_362_cout, fa_362_sum,
       fa_363_cout, fa_363_sum, fa_364_cout, fa_364_sum, fa_365_cout, fa_365_sum, fa_366_cout, fa_366_sum,
       fa_367_cout, fa_367_sum, fa_368_cout, fa_368_sum, fa_369_cout, fa_369_sum, fa_370_cout, fa_370_sum,
       fa_371_cout, fa_371_sum, fa_372_cout, fa_372_sum, fa_373_cout, fa_373_sum, fa_374_cout, fa_374_sum,
       fa_375_cout, fa_375_sum, fa_376_cout, fa_376_sum, fa_377_cout, fa_377_sum, fa_378_cout, fa_378_sum,
       fa_379_cout, fa_379_sum, fa_380_cout, fa_380_sum;

  or or_1 (C[20], A[20], B[20]);
  and and_1 (C[0], A[0], B[0]);
  and and_2 (and_2_out, A[1], B[0]);
  and and_3 (and_3_out, A[0], B[1]);
  FA fa_1 (.a(and_2_out), .b(and_3_out), .cin(1'b0), .sum(C[1]), .cout(fa_1_cout));
  and and_4 (and_4_out, A[2], B[0]);
  and and_5 (and_5_out, A[1], B[1]);
  FA fa_2 (.a(and_4_out), .b(and_5_out), .cin(fa_1_cout), .sum(fa_2_sum), .cout(fa_2_cout));
  and and_6 (and_6_out, A[0], B[2]);
  FA fa_3 (.a(fa_2_sum), .b(and_6_out), .cin(1'b0), .sum(C[2]), .cout(fa_3_cout));
  and and_7 (and_7_out, A[3], B[0]);
  and and_8 (and_8_out, A[2], B[1]);
  FA fa_4 (.a(and_7_out), .b(and_8_out), .cin(fa_2_cout), .sum(fa_4_sum), .cout(fa_4_cout));
  and and_9 (and_9_out, A[1], B[2]);
  FA fa_5 (.a(fa_4_sum), .b(and_9_out), .cin(fa_3_cout), .sum(fa_5_sum), .cout(fa_5_cout));
  and and_10 (and_10_out, A[0], B[3]);
  FA fa_6 (.a(fa_5_sum), .b(and_10_out), .cin(1'b0), .sum(C[3]), .cout(fa_6_cout));
  and and_11 (and_11_out, A[4], B[0]);
  and and_12 (and_12_out, A[3], B[1]);
  FA fa_7 (.a(and_11_out), .b(and_12_out), .cin(fa_4_cout), .sum(fa_7_sum), .cout(fa_7_cout));
  and and_13 (and_13_out, A[2], B[2]);
  FA fa_8 (.a(fa_7_sum), .b(and_13_out), .cin(fa_5_cout), .sum(fa_8_sum), .cout(fa_8_cout));
  and and_14 (and_14_out, A[1], B[3]);
  FA fa_9 (.a(fa_8_sum), .b(and_14_out), .cin(fa_6_cout), .sum(fa_9_sum), .cout(fa_9_cout));
  and and_15 (and_15_out, A[0], B[4]);
  FA fa_10 (.a(fa_9_sum), .b(and_15_out), .cin(1'b0), .sum(C[4]), .cout(fa_10_cout));
  and and_16 (and_16_out, A[5], B[0]);
  and and_17 (and_17_out, A[4], B[1]);
  FA fa_11 (.a(and_16_out), .b(and_17_out), .cin(fa_7_cout), .sum(fa_11_sum), .cout(fa_11_cout));
  and and_18 (and_18_out, A[3], B[2]);
  FA fa_12 (.a(fa_11_sum), .b(and_18_out), .cin(fa_8_cout), .sum(fa_12_sum), .cout(fa_12_cout));
  and and_19 (and_19_out, A[2], B[3]);
  FA fa_13 (.a(fa_12_sum), .b(and_19_out), .cin(fa_9_cout), .sum(fa_13_sum), .cout(fa_13_cout));
  and and_20 (and_20_out, A[1], B[4]);
  FA fa_14 (.a(fa_13_sum), .b(and_20_out), .cin(fa_10_cout), .sum(fa_14_sum), .cout(fa_14_cout));
  and and_21 (and_21_out, A[0], B[5]);
  FA fa_15 (.a(fa_14_sum), .b(and_21_out), .cin(1'b0), .sum(C[5]), .cout(fa_15_cout));
  and and_22 (and_22_out, A[6], B[0]);
  and and_23 (and_23_out, A[5], B[1]);
  FA fa_16 (.a(and_22_out), .b(and_23_out), .cin(fa_11_cout), .sum(fa_16_sum), .cout(fa_16_cout));
  and and_24 (and_24_out, A[4], B[2]);
  FA fa_17 (.a(fa_16_sum), .b(and_24_out), .cin(fa_12_cout), .sum(fa_17_sum), .cout(fa_17_cout));
  and and_25 (and_25_out, A[3], B[3]);
  FA fa_18 (.a(fa_17_sum), .b(and_25_out), .cin(fa_13_cout), .sum(fa_18_sum), .cout(fa_18_cout));
  and and_26 (and_26_out, A[2], B[4]);
  FA fa_19 (.a(fa_18_sum), .b(and_26_out), .cin(fa_14_cout), .sum(fa_19_sum), .cout(fa_19_cout));
  and and_27 (and_27_out, A[1], B[5]);
  FA fa_20 (.a(fa_19_sum), .b(and_27_out), .cin(fa_15_cout), .sum(fa_20_sum), .cout(fa_20_cout));
  and and_28 (and_28_out, A[0], B[6]);
  FA fa_21 (.a(fa_20_sum), .b(and_28_out), .cin(1'b0), .sum(C[6]), .cout(fa_21_cout));
  and and_29 (and_29_out, A[7], B[0]);
  and and_30 (and_30_out, A[6], B[1]);
  FA fa_22 (.a(and_29_out), .b(and_30_out), .cin(fa_16_cout), .sum(fa_22_sum), .cout(fa_22_cout));
  and and_31 (and_31_out, A[5], B[2]);
  FA fa_23 (.a(fa_22_sum), .b(and_31_out), .cin(fa_17_cout), .sum(fa_23_sum), .cout(fa_23_cout));
  and and_32 (and_32_out, A[4], B[3]);
  FA fa_24 (.a(fa_23_sum), .b(and_32_out), .cin(fa_18_cout), .sum(fa_24_sum), .cout(fa_24_cout));
  and and_33 (and_33_out, A[3], B[4]);
  FA fa_25 (.a(fa_24_sum), .b(and_33_out), .cin(fa_19_cout), .sum(fa_25_sum), .cout(fa_25_cout));
  and and_34 (and_34_out, A[2], B[5]);
  FA fa_26 (.a(fa_25_sum), .b(and_34_out), .cin(fa_20_cout), .sum(fa_26_sum), .cout(fa_26_cout));
  and and_35 (and_35_out, A[1], B[6]);
  FA fa_27 (.a(fa_26_sum), .b(and_35_out), .cin(fa_21_cout), .sum(fa_27_sum), .cout(fa_27_cout));
  and and_36 (and_36_out, A[0], B[7]);
  FA fa_28 (.a(fa_27_sum), .b(and_36_out), .cin(1'b0), .sum(C[7]), .cout(fa_28_cout));
  and and_37 (and_37_out, A[8], B[0]);
  and and_38 (and_38_out, A[7], B[1]);
  FA fa_29 (.a(and_37_out), .b(and_38_out), .cin(fa_22_cout), .sum(fa_29_sum), .cout(fa_29_cout));
  and and_39 (and_39_out, A[6], B[2]);
  FA fa_30 (.a(fa_29_sum), .b(and_39_out), .cin(fa_23_cout), .sum(fa_30_sum), .cout(fa_30_cout));
  and and_40 (and_40_out, A[5], B[3]);
  FA fa_31 (.a(fa_30_sum), .b(and_40_out), .cin(fa_24_cout), .sum(fa_31_sum), .cout(fa_31_cout));
  and and_41 (and_41_out, A[4], B[4]);
  FA fa_32 (.a(fa_31_sum), .b(and_41_out), .cin(fa_25_cout), .sum(fa_32_sum), .cout(fa_32_cout));
  and and_42 (and_42_out, A[3], B[5]);
  FA fa_33 (.a(fa_32_sum), .b(and_42_out), .cin(fa_26_cout), .sum(fa_33_sum), .cout(fa_33_cout));
  and and_43 (and_43_out, A[2], B[6]);
  FA fa_34 (.a(fa_33_sum), .b(and_43_out), .cin(fa_27_cout), .sum(fa_34_sum), .cout(fa_34_cout));
  and and_44 (and_44_out, A[1], B[7]);
  FA fa_35 (.a(fa_34_sum), .b(and_44_out), .cin(fa_28_cout), .sum(fa_35_sum), .cout(fa_35_cout));
  and and_45 (and_45_out, A[0], B[8]);
  FA fa_36 (.a(fa_35_sum), .b(and_45_out), .cin(1'b0), .sum(C[8]), .cout(fa_36_cout));
  and and_46 (and_46_out, A[9], B[0]);
  and and_47 (and_47_out, A[8], B[1]);
  FA fa_37 (.a(and_46_out), .b(and_47_out), .cin(fa_29_cout), .sum(fa_37_sum), .cout(fa_37_cout));
  and and_48 (and_48_out, A[7], B[2]);
  FA fa_38 (.a(fa_37_sum), .b(and_48_out), .cin(fa_30_cout), .sum(fa_38_sum), .cout(fa_38_cout));
  and and_49 (and_49_out, A[6], B[3]);
  FA fa_39 (.a(fa_38_sum), .b(and_49_out), .cin(fa_31_cout), .sum(fa_39_sum), .cout(fa_39_cout));
  and and_50 (and_50_out, A[5], B[4]);
  FA fa_40 (.a(fa_39_sum), .b(and_50_out), .cin(fa_32_cout), .sum(fa_40_sum), .cout(fa_40_cout));
  and and_51 (and_51_out, A[4], B[5]);
  FA fa_41 (.a(fa_40_sum), .b(and_51_out), .cin(fa_33_cout), .sum(fa_41_sum), .cout(fa_41_cout));
  and and_52 (and_52_out, A[3], B[6]);
  FA fa_42 (.a(fa_41_sum), .b(and_52_out), .cin(fa_34_cout), .sum(fa_42_sum), .cout(fa_42_cout));
  and and_53 (and_53_out, A[2], B[7]);
  FA fa_43 (.a(fa_42_sum), .b(and_53_out), .cin(fa_35_cout), .sum(fa_43_sum), .cout(fa_43_cout));
  and and_54 (and_54_out, A[1], B[8]);
  FA fa_44 (.a(fa_43_sum), .b(and_54_out), .cin(fa_36_cout), .sum(fa_44_sum), .cout(fa_44_cout));
  and and_55 (and_55_out, A[0], B[9]);
  FA fa_45 (.a(fa_44_sum), .b(and_55_out), .cin(1'b0), .sum(C[9]), .cout(fa_45_cout));
  and and_56 (and_56_out, A[10], B[0]);
  and and_57 (and_57_out, A[9], B[1]);
  FA fa_46 (.a(and_56_out), .b(and_57_out), .cin(fa_37_cout), .sum(fa_46_sum), .cout(fa_46_cout));
  and and_58 (and_58_out, A[8], B[2]);
  FA fa_47 (.a(fa_46_sum), .b(and_58_out), .cin(fa_38_cout), .sum(fa_47_sum), .cout(fa_47_cout));
  and and_59 (and_59_out, A[7], B[3]);
  FA fa_48 (.a(fa_47_sum), .b(and_59_out), .cin(fa_39_cout), .sum(fa_48_sum), .cout(fa_48_cout));
  and and_60 (and_60_out, A[6], B[4]);
  FA fa_49 (.a(fa_48_sum), .b(and_60_out), .cin(fa_40_cout), .sum(fa_49_sum), .cout(fa_49_cout));
  and and_61 (and_61_out, A[5], B[5]);
  FA fa_50 (.a(fa_49_sum), .b(and_61_out), .cin(fa_41_cout), .sum(fa_50_sum), .cout(fa_50_cout));
  and and_62 (and_62_out, A[4], B[6]);
  FA fa_51 (.a(fa_50_sum), .b(and_62_out), .cin(fa_42_cout), .sum(fa_51_sum), .cout(fa_51_cout));
  and and_63 (and_63_out, A[3], B[7]);
  FA fa_52 (.a(fa_51_sum), .b(and_63_out), .cin(fa_43_cout), .sum(fa_52_sum), .cout(fa_52_cout));
  and and_64 (and_64_out, A[2], B[8]);
  FA fa_53 (.a(fa_52_sum), .b(and_64_out), .cin(fa_44_cout), .sum(fa_53_sum), .cout(fa_53_cout));
  and and_65 (and_65_out, A[1], B[9]);
  FA fa_54 (.a(fa_53_sum), .b(and_65_out), .cin(fa_45_cout), .sum(fa_54_sum), .cout(fa_54_cout));
  and and_66 (and_66_out, A[0], B[10]);
  FA fa_55 (.a(fa_54_sum), .b(and_66_out), .cin(1'b0), .sum(C[10]), .cout(fa_55_cout));
  and and_67 (and_67_out, A[11], B[0]);
  and and_68 (and_68_out, A[10], B[1]);
  FA fa_56 (.a(and_67_out), .b(and_68_out), .cin(fa_46_cout), .sum(fa_56_sum), .cout(fa_56_cout));
  and and_69 (and_69_out, A[9], B[2]);
  FA fa_57 (.a(fa_56_sum), .b(and_69_out), .cin(fa_47_cout), .sum(fa_57_sum), .cout(fa_57_cout));
  and and_70 (and_70_out, A[8], B[3]);
  FA fa_58 (.a(fa_57_sum), .b(and_70_out), .cin(fa_48_cout), .sum(fa_58_sum), .cout(fa_58_cout));
  and and_71 (and_71_out, A[7], B[4]);
  FA fa_59 (.a(fa_58_sum), .b(and_71_out), .cin(fa_49_cout), .sum(fa_59_sum), .cout(fa_59_cout));
  and and_72 (and_72_out, A[6], B[5]);
  FA fa_60 (.a(fa_59_sum), .b(and_72_out), .cin(fa_50_cout), .sum(fa_60_sum), .cout(fa_60_cout));
  and and_73 (and_73_out, A[5], B[6]);
  FA fa_61 (.a(fa_60_sum), .b(and_73_out), .cin(fa_51_cout), .sum(fa_61_sum), .cout(fa_61_cout));
  and and_74 (and_74_out, A[4], B[7]);
  FA fa_62 (.a(fa_61_sum), .b(and_74_out), .cin(fa_52_cout), .sum(fa_62_sum), .cout(fa_62_cout));
  and and_75 (and_75_out, A[3], B[8]);
  FA fa_63 (.a(fa_62_sum), .b(and_75_out), .cin(fa_53_cout), .sum(fa_63_sum), .cout(fa_63_cout));
  and and_76 (and_76_out, A[2], B[9]);
  FA fa_64 (.a(fa_63_sum), .b(and_76_out), .cin(fa_54_cout), .sum(fa_64_sum), .cout(fa_64_cout));
  and and_77 (and_77_out, A[1], B[10]);
  FA fa_65 (.a(fa_64_sum), .b(and_77_out), .cin(fa_55_cout), .sum(fa_65_sum), .cout(fa_65_cout));
  and and_78 (and_78_out, A[0], B[11]);
  FA fa_66 (.a(fa_65_sum), .b(and_78_out), .cin(1'b0), .sum(C[11]), .cout(fa_66_cout));
  and and_79 (and_79_out, A[12], B[0]);
  and and_80 (and_80_out, A[11], B[1]);
  FA fa_67 (.a(and_79_out), .b(and_80_out), .cin(fa_56_cout), .sum(fa_67_sum), .cout(fa_67_cout));
  and and_81 (and_81_out, A[10], B[2]);
  FA fa_68 (.a(fa_67_sum), .b(and_81_out), .cin(fa_57_cout), .sum(fa_68_sum), .cout(fa_68_cout));
  and and_82 (and_82_out, A[9], B[3]);
  FA fa_69 (.a(fa_68_sum), .b(and_82_out), .cin(fa_58_cout), .sum(fa_69_sum), .cout(fa_69_cout));
  and and_83 (and_83_out, A[8], B[4]);
  FA fa_70 (.a(fa_69_sum), .b(and_83_out), .cin(fa_59_cout), .sum(fa_70_sum), .cout(fa_70_cout));
  and and_84 (and_84_out, A[7], B[5]);
  FA fa_71 (.a(fa_70_sum), .b(and_84_out), .cin(fa_60_cout), .sum(fa_71_sum), .cout(fa_71_cout));
  and and_85 (and_85_out, A[6], B[6]);
  FA fa_72 (.a(fa_71_sum), .b(and_85_out), .cin(fa_61_cout), .sum(fa_72_sum), .cout(fa_72_cout));
  and and_86 (and_86_out, A[5], B[7]);
  FA fa_73 (.a(fa_72_sum), .b(and_86_out), .cin(fa_62_cout), .sum(fa_73_sum), .cout(fa_73_cout));
  and and_87 (and_87_out, A[4], B[8]);
  FA fa_74 (.a(fa_73_sum), .b(and_87_out), .cin(fa_63_cout), .sum(fa_74_sum), .cout(fa_74_cout));
  and and_88 (and_88_out, A[3], B[9]);
  FA fa_75 (.a(fa_74_sum), .b(and_88_out), .cin(fa_64_cout), .sum(fa_75_sum), .cout(fa_75_cout));
  and and_89 (and_89_out, A[2], B[10]);
  FA fa_76 (.a(fa_75_sum), .b(and_89_out), .cin(fa_65_cout), .sum(fa_76_sum), .cout(fa_76_cout));
  and and_90 (and_90_out, A[1], B[11]);
  FA fa_77 (.a(fa_76_sum), .b(and_90_out), .cin(fa_66_cout), .sum(fa_77_sum), .cout(fa_77_cout));
  and and_91 (and_91_out, A[0], B[12]);
  FA fa_78 (.a(fa_77_sum), .b(and_91_out), .cin(1'b0), .sum(C[12]), .cout(fa_78_cout));
  and and_92 (and_92_out, A[13], B[0]);
  and and_93 (and_93_out, A[12], B[1]);
  FA fa_79 (.a(and_92_out), .b(and_93_out), .cin(fa_67_cout), .sum(fa_79_sum), .cout(fa_79_cout));
  and and_94 (and_94_out, A[11], B[2]);
  FA fa_80 (.a(fa_79_sum), .b(and_94_out), .cin(fa_68_cout), .sum(fa_80_sum), .cout(fa_80_cout));
  and and_95 (and_95_out, A[10], B[3]);
  FA fa_81 (.a(fa_80_sum), .b(and_95_out), .cin(fa_69_cout), .sum(fa_81_sum), .cout(fa_81_cout));
  and and_96 (and_96_out, A[9], B[4]);
  FA fa_82 (.a(fa_81_sum), .b(and_96_out), .cin(fa_70_cout), .sum(fa_82_sum), .cout(fa_82_cout));
  and and_97 (and_97_out, A[8], B[5]);
  FA fa_83 (.a(fa_82_sum), .b(and_97_out), .cin(fa_71_cout), .sum(fa_83_sum), .cout(fa_83_cout));
  and and_98 (and_98_out, A[7], B[6]);
  FA fa_84 (.a(fa_83_sum), .b(and_98_out), .cin(fa_72_cout), .sum(fa_84_sum), .cout(fa_84_cout));
  and and_99 (and_99_out, A[6], B[7]);
  FA fa_85 (.a(fa_84_sum), .b(and_99_out), .cin(fa_73_cout), .sum(fa_85_sum), .cout(fa_85_cout));
  and and_100 (and_100_out, A[5], B[8]);
  FA fa_86 (.a(fa_85_sum), .b(and_100_out), .cin(fa_74_cout), .sum(fa_86_sum), .cout(fa_86_cout));
  and and_101 (and_101_out, A[4], B[9]);
  FA fa_87 (.a(fa_86_sum), .b(and_101_out), .cin(fa_75_cout), .sum(fa_87_sum), .cout(fa_87_cout));
  and and_102 (and_102_out, A[3], B[10]);
  FA fa_88 (.a(fa_87_sum), .b(and_102_out), .cin(fa_76_cout), .sum(fa_88_sum), .cout(fa_88_cout));
  and and_103 (and_103_out, A[2], B[11]);
  FA fa_89 (.a(fa_88_sum), .b(and_103_out), .cin(fa_77_cout), .sum(fa_89_sum), .cout(fa_89_cout));
  and and_104 (and_104_out, A[1], B[12]);
  FA fa_90 (.a(fa_89_sum), .b(and_104_out), .cin(fa_78_cout), .sum(fa_90_sum), .cout(fa_90_cout));
  and and_105 (and_105_out, A[0], B[13]);
  FA fa_91 (.a(fa_90_sum), .b(and_105_out), .cin(1'b0), .sum(C[13]), .cout(fa_91_cout));
  and and_106 (and_106_out, A[14], B[0]);
  and and_107 (and_107_out, A[13], B[1]);
  FA fa_92 (.a(and_106_out), .b(and_107_out), .cin(fa_79_cout), .sum(fa_92_sum), .cout(fa_92_cout));
  and and_108 (and_108_out, A[12], B[2]);
  FA fa_93 (.a(fa_92_sum), .b(and_108_out), .cin(fa_80_cout), .sum(fa_93_sum), .cout(fa_93_cout));
  and and_109 (and_109_out, A[11], B[3]);
  FA fa_94 (.a(fa_93_sum), .b(and_109_out), .cin(fa_81_cout), .sum(fa_94_sum), .cout(fa_94_cout));
  and and_110 (and_110_out, A[10], B[4]);
  FA fa_95 (.a(fa_94_sum), .b(and_110_out), .cin(fa_82_cout), .sum(fa_95_sum), .cout(fa_95_cout));
  and and_111 (and_111_out, A[9], B[5]);
  FA fa_96 (.a(fa_95_sum), .b(and_111_out), .cin(fa_83_cout), .sum(fa_96_sum), .cout(fa_96_cout));
  and and_112 (and_112_out, A[8], B[6]);
  FA fa_97 (.a(fa_96_sum), .b(and_112_out), .cin(fa_84_cout), .sum(fa_97_sum), .cout(fa_97_cout));
  and and_113 (and_113_out, A[7], B[7]);
  FA fa_98 (.a(fa_97_sum), .b(and_113_out), .cin(fa_85_cout), .sum(fa_98_sum), .cout(fa_98_cout));
  and and_114 (and_114_out, A[6], B[8]);
  FA fa_99 (.a(fa_98_sum), .b(and_114_out), .cin(fa_86_cout), .sum(fa_99_sum), .cout(fa_99_cout));
  and and_115 (and_115_out, A[5], B[9]);
  FA fa_100 (.a(fa_99_sum), .b(and_115_out), .cin(fa_87_cout), .sum(fa_100_sum), .cout(fa_100_cout));
  and and_116 (and_116_out, A[4], B[10]);
  FA fa_101 (.a(fa_100_sum), .b(and_116_out), .cin(fa_88_cout), .sum(fa_101_sum), .cout(fa_101_cout));
  and and_117 (and_117_out, A[3], B[11]);
  FA fa_102 (.a(fa_101_sum), .b(and_117_out), .cin(fa_89_cout), .sum(fa_102_sum), .cout(fa_102_cout));
  and and_118 (and_118_out, A[2], B[12]);
  FA fa_103 (.a(fa_102_sum), .b(and_118_out), .cin(fa_90_cout), .sum(fa_103_sum), .cout(fa_103_cout));
  and and_119 (and_119_out, A[1], B[13]);
  FA fa_104 (.a(fa_103_sum), .b(and_119_out), .cin(fa_91_cout), .sum(fa_104_sum), .cout(fa_104_cout));
  and and_120 (and_120_out, A[0], B[14]);
  FA fa_105 (.a(fa_104_sum), .b(and_120_out), .cin(1'b0), .sum(C[14]), .cout(fa_105_cout));
  and and_121 (and_121_out, A[15], B[0]);
  and and_122 (and_122_out, A[14], B[1]);
  FA fa_106 (.a(and_121_out), .b(and_122_out), .cin(fa_92_cout), .sum(fa_106_sum), .cout(fa_106_cout));
  and and_123 (and_123_out, A[13], B[2]);
  FA fa_107 (.a(fa_106_sum), .b(and_123_out), .cin(fa_93_cout), .sum(fa_107_sum), .cout(fa_107_cout));
  and and_124 (and_124_out, A[12], B[3]);
  FA fa_108 (.a(fa_107_sum), .b(and_124_out), .cin(fa_94_cout), .sum(fa_108_sum), .cout(fa_108_cout));
  and and_125 (and_125_out, A[11], B[4]);
  FA fa_109 (.a(fa_108_sum), .b(and_125_out), .cin(fa_95_cout), .sum(fa_109_sum), .cout(fa_109_cout));
  and and_126 (and_126_out, A[10], B[5]);
  FA fa_110 (.a(fa_109_sum), .b(and_126_out), .cin(fa_96_cout), .sum(fa_110_sum), .cout(fa_110_cout));
  and and_127 (and_127_out, A[9], B[6]);
  FA fa_111 (.a(fa_110_sum), .b(and_127_out), .cin(fa_97_cout), .sum(fa_111_sum), .cout(fa_111_cout));
  and and_128 (and_128_out, A[8], B[7]);
  FA fa_112 (.a(fa_111_sum), .b(and_128_out), .cin(fa_98_cout), .sum(fa_112_sum), .cout(fa_112_cout));
  and and_129 (and_129_out, A[7], B[8]);
  FA fa_113 (.a(fa_112_sum), .b(and_129_out), .cin(fa_99_cout), .sum(fa_113_sum), .cout(fa_113_cout));
  and and_130 (and_130_out, A[6], B[9]);
  FA fa_114 (.a(fa_113_sum), .b(and_130_out), .cin(fa_100_cout), .sum(fa_114_sum), .cout(fa_114_cout));
  and and_131 (and_131_out, A[5], B[10]);
  FA fa_115 (.a(fa_114_sum), .b(and_131_out), .cin(fa_101_cout), .sum(fa_115_sum), .cout(fa_115_cout));
  and and_132 (and_132_out, A[4], B[11]);
  FA fa_116 (.a(fa_115_sum), .b(and_132_out), .cin(fa_102_cout), .sum(fa_116_sum), .cout(fa_116_cout));
  and and_133 (and_133_out, A[3], B[12]);
  FA fa_117 (.a(fa_116_sum), .b(and_133_out), .cin(fa_103_cout), .sum(fa_117_sum), .cout(fa_117_cout));
  and and_134 (and_134_out, A[2], B[13]);
  FA fa_118 (.a(fa_117_sum), .b(and_134_out), .cin(fa_104_cout), .sum(fa_118_sum), .cout(fa_118_cout));
  and and_135 (and_135_out, A[1], B[14]);
  FA fa_119 (.a(fa_118_sum), .b(and_135_out), .cin(fa_105_cout), .sum(fa_119_sum), .cout(fa_119_cout));
  and and_136 (and_136_out, A[0], B[15]);
  FA fa_120 (.a(fa_119_sum), .b(and_136_out), .cin(1'b0), .sum(C[15]), .cout(fa_120_cout));
  and and_137 (and_137_out, A[16], B[0]);
  and and_138 (and_138_out, A[15], B[1]);
  FA fa_121 (.a(and_137_out), .b(and_138_out), .cin(fa_106_cout), .sum(fa_121_sum), .cout(fa_121_cout));
  and and_139 (and_139_out, A[14], B[2]);
  FA fa_122 (.a(fa_121_sum), .b(and_139_out), .cin(fa_107_cout), .sum(fa_122_sum), .cout(fa_122_cout));
  and and_140 (and_140_out, A[13], B[3]);
  FA fa_123 (.a(fa_122_sum), .b(and_140_out), .cin(fa_108_cout), .sum(fa_123_sum), .cout(fa_123_cout));
  and and_141 (and_141_out, A[12], B[4]);
  FA fa_124 (.a(fa_123_sum), .b(and_141_out), .cin(fa_109_cout), .sum(fa_124_sum), .cout(fa_124_cout));
  and and_142 (and_142_out, A[11], B[5]);
  FA fa_125 (.a(fa_124_sum), .b(and_142_out), .cin(fa_110_cout), .sum(fa_125_sum), .cout(fa_125_cout));
  and and_143 (and_143_out, A[10], B[6]);
  FA fa_126 (.a(fa_125_sum), .b(and_143_out), .cin(fa_111_cout), .sum(fa_126_sum), .cout(fa_126_cout));
  and and_144 (and_144_out, A[9], B[7]);
  FA fa_127 (.a(fa_126_sum), .b(and_144_out), .cin(fa_112_cout), .sum(fa_127_sum), .cout(fa_127_cout));
  and and_145 (and_145_out, A[8], B[8]);
  FA fa_128 (.a(fa_127_sum), .b(and_145_out), .cin(fa_113_cout), .sum(fa_128_sum), .cout(fa_128_cout));
  and and_146 (and_146_out, A[7], B[9]);
  FA fa_129 (.a(fa_128_sum), .b(and_146_out), .cin(fa_114_cout), .sum(fa_129_sum), .cout(fa_129_cout));
  and and_147 (and_147_out, A[6], B[10]);
  FA fa_130 (.a(fa_129_sum), .b(and_147_out), .cin(fa_115_cout), .sum(fa_130_sum), .cout(fa_130_cout));
  and and_148 (and_148_out, A[5], B[11]);
  FA fa_131 (.a(fa_130_sum), .b(and_148_out), .cin(fa_116_cout), .sum(fa_131_sum), .cout(fa_131_cout));
  and and_149 (and_149_out, A[4], B[12]);
  FA fa_132 (.a(fa_131_sum), .b(and_149_out), .cin(fa_117_cout), .sum(fa_132_sum), .cout(fa_132_cout));
  and and_150 (and_150_out, A[3], B[13]);
  FA fa_133 (.a(fa_132_sum), .b(and_150_out), .cin(fa_118_cout), .sum(fa_133_sum), .cout(fa_133_cout));
  and and_151 (and_151_out, A[2], B[14]);
  FA fa_134 (.a(fa_133_sum), .b(and_151_out), .cin(fa_119_cout), .sum(fa_134_sum), .cout(fa_134_cout));
  and and_152 (and_152_out, A[1], B[15]);
  FA fa_135 (.a(fa_134_sum), .b(and_152_out), .cin(fa_120_cout), .sum(fa_135_sum), .cout(fa_135_cout));
  and and_153 (and_153_out, A[0], B[16]);
  FA fa_136 (.a(fa_135_sum), .b(and_153_out), .cin(1'b0), .sum(C[16]), .cout(fa_136_cout));
  and and_154 (and_154_out, A[17], B[0]);
  and and_155 (and_155_out, A[16], B[1]);
  FA fa_137 (.a(and_154_out), .b(and_155_out), .cin(fa_121_cout), .sum(fa_137_sum), .cout(fa_137_cout));
  and and_156 (and_156_out, A[15], B[2]);
  FA fa_138 (.a(fa_137_sum), .b(and_156_out), .cin(fa_122_cout), .sum(fa_138_sum), .cout(fa_138_cout));
  and and_157 (and_157_out, A[14], B[3]);
  FA fa_139 (.a(fa_138_sum), .b(and_157_out), .cin(fa_123_cout), .sum(fa_139_sum), .cout(fa_139_cout));
  and and_158 (and_158_out, A[13], B[4]);
  FA fa_140 (.a(fa_139_sum), .b(and_158_out), .cin(fa_124_cout), .sum(fa_140_sum), .cout(fa_140_cout));
  and and_159 (and_159_out, A[12], B[5]);
  FA fa_141 (.a(fa_140_sum), .b(and_159_out), .cin(fa_125_cout), .sum(fa_141_sum), .cout(fa_141_cout));
  and and_160 (and_160_out, A[11], B[6]);
  FA fa_142 (.a(fa_141_sum), .b(and_160_out), .cin(fa_126_cout), .sum(fa_142_sum), .cout(fa_142_cout));
  and and_161 (and_161_out, A[10], B[7]);
  FA fa_143 (.a(fa_142_sum), .b(and_161_out), .cin(fa_127_cout), .sum(fa_143_sum), .cout(fa_143_cout));
  and and_162 (and_162_out, A[9], B[8]);
  FA fa_144 (.a(fa_143_sum), .b(and_162_out), .cin(fa_128_cout), .sum(fa_144_sum), .cout(fa_144_cout));
  and and_163 (and_163_out, A[8], B[9]);
  FA fa_145 (.a(fa_144_sum), .b(and_163_out), .cin(fa_129_cout), .sum(fa_145_sum), .cout(fa_145_cout));
  and and_164 (and_164_out, A[7], B[10]);
  FA fa_146 (.a(fa_145_sum), .b(and_164_out), .cin(fa_130_cout), .sum(fa_146_sum), .cout(fa_146_cout));
  and and_165 (and_165_out, A[6], B[11]);
  FA fa_147 (.a(fa_146_sum), .b(and_165_out), .cin(fa_131_cout), .sum(fa_147_sum), .cout(fa_147_cout));
  and and_166 (and_166_out, A[5], B[12]);
  FA fa_148 (.a(fa_147_sum), .b(and_166_out), .cin(fa_132_cout), .sum(fa_148_sum), .cout(fa_148_cout));
  and and_167 (and_167_out, A[4], B[13]);
  FA fa_149 (.a(fa_148_sum), .b(and_167_out), .cin(fa_133_cout), .sum(fa_149_sum), .cout(fa_149_cout));
  and and_168 (and_168_out, A[3], B[14]);
  FA fa_150 (.a(fa_149_sum), .b(and_168_out), .cin(fa_134_cout), .sum(fa_150_sum), .cout(fa_150_cout));
  and and_169 (and_169_out, A[2], B[15]);
  FA fa_151 (.a(fa_150_sum), .b(and_169_out), .cin(fa_135_cout), .sum(fa_151_sum), .cout(fa_151_cout));
  and and_170 (and_170_out, A[1], B[16]);
  FA fa_152 (.a(fa_151_sum), .b(and_170_out), .cin(fa_136_cout), .sum(fa_152_sum), .cout(fa_152_cout));
  and and_171 (and_171_out, A[0], B[17]);
  FA fa_153 (.a(fa_152_sum), .b(and_171_out), .cin(1'b0), .sum(C[17]), .cout(fa_153_cout));
  and and_172 (and_172_out, A[18], B[0]);
  and and_173 (and_173_out, A[17], B[1]);
  FA fa_154 (.a(and_172_out), .b(and_173_out), .cin(fa_137_cout), .sum(fa_154_sum), .cout(fa_154_cout));
  and and_174 (and_174_out, A[16], B[2]);
  FA fa_155 (.a(fa_154_sum), .b(and_174_out), .cin(fa_138_cout), .sum(fa_155_sum), .cout(fa_155_cout));
  and and_175 (and_175_out, A[15], B[3]);
  FA fa_156 (.a(fa_155_sum), .b(and_175_out), .cin(fa_139_cout), .sum(fa_156_sum), .cout(fa_156_cout));
  and and_176 (and_176_out, A[14], B[4]);
  FA fa_157 (.a(fa_156_sum), .b(and_176_out), .cin(fa_140_cout), .sum(fa_157_sum), .cout(fa_157_cout));
  and and_177 (and_177_out, A[13], B[5]);
  FA fa_158 (.a(fa_157_sum), .b(and_177_out), .cin(fa_141_cout), .sum(fa_158_sum), .cout(fa_158_cout));
  and and_178 (and_178_out, A[12], B[6]);
  FA fa_159 (.a(fa_158_sum), .b(and_178_out), .cin(fa_142_cout), .sum(fa_159_sum), .cout(fa_159_cout));
  and and_179 (and_179_out, A[11], B[7]);
  FA fa_160 (.a(fa_159_sum), .b(and_179_out), .cin(fa_143_cout), .sum(fa_160_sum), .cout(fa_160_cout));
  and and_180 (and_180_out, A[10], B[8]);
  FA fa_161 (.a(fa_160_sum), .b(and_180_out), .cin(fa_144_cout), .sum(fa_161_sum), .cout(fa_161_cout));
  and and_181 (and_181_out, A[9], B[9]);
  FA fa_162 (.a(fa_161_sum), .b(and_181_out), .cin(fa_145_cout), .sum(fa_162_sum), .cout(fa_162_cout));
  and and_182 (and_182_out, A[8], B[10]);
  FA fa_163 (.a(fa_162_sum), .b(and_182_out), .cin(fa_146_cout), .sum(fa_163_sum), .cout(fa_163_cout));
  and and_183 (and_183_out, A[7], B[11]);
  FA fa_164 (.a(fa_163_sum), .b(and_183_out), .cin(fa_147_cout), .sum(fa_164_sum), .cout(fa_164_cout));
  and and_184 (and_184_out, A[6], B[12]);
  FA fa_165 (.a(fa_164_sum), .b(and_184_out), .cin(fa_148_cout), .sum(fa_165_sum), .cout(fa_165_cout));
  and and_185 (and_185_out, A[5], B[13]);
  FA fa_166 (.a(fa_165_sum), .b(and_185_out), .cin(fa_149_cout), .sum(fa_166_sum), .cout(fa_166_cout));
  and and_186 (and_186_out, A[4], B[14]);
  FA fa_167 (.a(fa_166_sum), .b(and_186_out), .cin(fa_150_cout), .sum(fa_167_sum), .cout(fa_167_cout));
  and and_187 (and_187_out, A[3], B[15]);
  FA fa_168 (.a(fa_167_sum), .b(and_187_out), .cin(fa_151_cout), .sum(fa_168_sum), .cout(fa_168_cout));
  and and_188 (and_188_out, A[2], B[16]);
  FA fa_169 (.a(fa_168_sum), .b(and_188_out), .cin(fa_152_cout), .sum(fa_169_sum), .cout(fa_169_cout));
  and and_189 (and_189_out, A[1], B[17]);
  FA fa_170 (.a(fa_169_sum), .b(and_189_out), .cin(fa_153_cout), .sum(fa_170_sum), .cout(fa_170_cout));
  and and_190 (and_190_out, A[0], B[18]);
  FA fa_171 (.a(fa_170_sum), .b(and_190_out), .cin(1'b0), .sum(C[18]), .cout(fa_171_cout));
  and and_191 (and_191_out, A[19], B[0]);
  and and_192 (and_192_out, A[18], B[1]);
  FA fa_172 (.a(and_191_out), .b(and_192_out), .cin(fa_154_cout), .sum(fa_172_sum), .cout(fa_172_cout));
  and and_193 (and_193_out, A[17], B[2]);
  FA fa_173 (.a(fa_172_sum), .b(and_193_out), .cin(fa_155_cout), .sum(fa_173_sum), .cout(fa_173_cout));
  and and_194 (and_194_out, A[16], B[3]);
  FA fa_174 (.a(fa_173_sum), .b(and_194_out), .cin(fa_156_cout), .sum(fa_174_sum), .cout(fa_174_cout));
  and and_195 (and_195_out, A[15], B[4]);
  FA fa_175 (.a(fa_174_sum), .b(and_195_out), .cin(fa_157_cout), .sum(fa_175_sum), .cout(fa_175_cout));
  and and_196 (and_196_out, A[14], B[5]);
  FA fa_176 (.a(fa_175_sum), .b(and_196_out), .cin(fa_158_cout), .sum(fa_176_sum), .cout(fa_176_cout));
  and and_197 (and_197_out, A[13], B[6]);
  FA fa_177 (.a(fa_176_sum), .b(and_197_out), .cin(fa_159_cout), .sum(fa_177_sum), .cout(fa_177_cout));
  and and_198 (and_198_out, A[12], B[7]);
  FA fa_178 (.a(fa_177_sum), .b(and_198_out), .cin(fa_160_cout), .sum(fa_178_sum), .cout(fa_178_cout));
  and and_199 (and_199_out, A[11], B[8]);
  FA fa_179 (.a(fa_178_sum), .b(and_199_out), .cin(fa_161_cout), .sum(fa_179_sum), .cout(fa_179_cout));
  and and_200 (and_200_out, A[10], B[9]);
  FA fa_180 (.a(fa_179_sum), .b(and_200_out), .cin(fa_162_cout), .sum(fa_180_sum), .cout(fa_180_cout));
  and and_201 (and_201_out, A[9], B[10]);
  FA fa_181 (.a(fa_180_sum), .b(and_201_out), .cin(fa_163_cout), .sum(fa_181_sum), .cout(fa_181_cout));
  and and_202 (and_202_out, A[8], B[11]);
  FA fa_182 (.a(fa_181_sum), .b(and_202_out), .cin(fa_164_cout), .sum(fa_182_sum), .cout(fa_182_cout));
  and and_203 (and_203_out, A[7], B[12]);
  FA fa_183 (.a(fa_182_sum), .b(and_203_out), .cin(fa_165_cout), .sum(fa_183_sum), .cout(fa_183_cout));
  and and_204 (and_204_out, A[6], B[13]);
  FA fa_184 (.a(fa_183_sum), .b(and_204_out), .cin(fa_166_cout), .sum(fa_184_sum), .cout(fa_184_cout));
  and and_205 (and_205_out, A[5], B[14]);
  FA fa_185 (.a(fa_184_sum), .b(and_205_out), .cin(fa_167_cout), .sum(fa_185_sum), .cout(fa_185_cout));
  and and_206 (and_206_out, A[4], B[15]);
  FA fa_186 (.a(fa_185_sum), .b(and_206_out), .cin(fa_168_cout), .sum(fa_186_sum), .cout(fa_186_cout));
  and and_207 (and_207_out, A[3], B[16]);
  FA fa_187 (.a(fa_186_sum), .b(and_207_out), .cin(fa_169_cout), .sum(fa_187_sum), .cout(fa_187_cout));
  and and_208 (and_208_out, A[2], B[17]);
  FA fa_188 (.a(fa_187_sum), .b(and_208_out), .cin(fa_170_cout), .sum(fa_188_sum), .cout(fa_188_cout));
  and and_209 (and_209_out, A[1], B[18]);
  FA fa_189 (.a(fa_188_sum), .b(and_209_out), .cin(fa_171_cout), .sum(fa_189_sum), .cout(fa_189_cout));
  and and_210 (and_210_out, A[0], B[19]);
  FA fa_190 (.a(fa_189_sum), .b(and_210_out), .cin(1'b0), .sum(C[19]), .cout(fa_190_cout));
  and and_211 (and_211_out, A[19], B[1]);
  FA fa_191 (.a(1'b0), .b(and_211_out), .cin(fa_172_cout), .sum(fa_191_sum), .cout(fa_191_cout));
  and and_212 (and_212_out, A[18], B[2]);
  FA fa_192 (.a(fa_191_sum), .b(and_212_out), .cin(fa_173_cout), .sum(fa_192_sum), .cout(fa_192_cout));
  and and_213 (and_213_out, A[17], B[3]);
  FA fa_193 (.a(fa_192_sum), .b(and_213_out), .cin(fa_174_cout), .sum(fa_193_sum), .cout(fa_193_cout));
  and and_214 (and_214_out, A[16], B[4]);
  FA fa_194 (.a(fa_193_sum), .b(and_214_out), .cin(fa_175_cout), .sum(fa_194_sum), .cout(fa_194_cout));
  and and_215 (and_215_out, A[15], B[5]);
  FA fa_195 (.a(fa_194_sum), .b(and_215_out), .cin(fa_176_cout), .sum(fa_195_sum), .cout(fa_195_cout));
  and and_216 (and_216_out, A[14], B[6]);
  FA fa_196 (.a(fa_195_sum), .b(and_216_out), .cin(fa_177_cout), .sum(fa_196_sum), .cout(fa_196_cout));
  and and_217 (and_217_out, A[13], B[7]);
  FA fa_197 (.a(fa_196_sum), .b(and_217_out), .cin(fa_178_cout), .sum(fa_197_sum), .cout(fa_197_cout));
  and and_218 (and_218_out, A[12], B[8]);
  FA fa_198 (.a(fa_197_sum), .b(and_218_out), .cin(fa_179_cout), .sum(fa_198_sum), .cout(fa_198_cout));
  and and_219 (and_219_out, A[11], B[9]);
  FA fa_199 (.a(fa_198_sum), .b(and_219_out), .cin(fa_180_cout), .sum(fa_199_sum), .cout(fa_199_cout));
  and and_220 (and_220_out, A[10], B[10]);
  FA fa_200 (.a(fa_199_sum), .b(and_220_out), .cin(fa_181_cout), .sum(fa_200_sum), .cout(fa_200_cout));
  and and_221 (and_221_out, A[9], B[11]);
  FA fa_201 (.a(fa_200_sum), .b(and_221_out), .cin(fa_182_cout), .sum(fa_201_sum), .cout(fa_201_cout));
  and and_222 (and_222_out, A[8], B[12]);
  FA fa_202 (.a(fa_201_sum), .b(and_222_out), .cin(fa_183_cout), .sum(fa_202_sum), .cout(fa_202_cout));
  and and_223 (and_223_out, A[7], B[13]);
  FA fa_203 (.a(fa_202_sum), .b(and_223_out), .cin(fa_184_cout), .sum(fa_203_sum), .cout(fa_203_cout));
  and and_224 (and_224_out, A[6], B[14]);
  FA fa_204 (.a(fa_203_sum), .b(and_224_out), .cin(fa_185_cout), .sum(fa_204_sum), .cout(fa_204_cout));
  and and_225 (and_225_out, A[5], B[15]);
  FA fa_205 (.a(fa_204_sum), .b(and_225_out), .cin(fa_186_cout), .sum(fa_205_sum), .cout(fa_205_cout));
  and and_226 (and_226_out, A[4], B[16]);
  FA fa_206 (.a(fa_205_sum), .b(and_226_out), .cin(fa_187_cout), .sum(fa_206_sum), .cout(fa_206_cout));
  and and_227 (and_227_out, A[3], B[17]);
  FA fa_207 (.a(fa_206_sum), .b(and_227_out), .cin(fa_188_cout), .sum(fa_207_sum), .cout(fa_207_cout));
  and and_228 (and_228_out, A[2], B[18]);
  FA fa_208 (.a(fa_207_sum), .b(and_228_out), .cin(fa_189_cout), .sum(fa_208_sum), .cout(fa_208_cout));
  and and_229 (and_229_out, A[1], B[19]);
  FA fa_209 (.a(fa_208_sum), .b(and_229_out), .cin(fa_190_cout), .sum(fa_209_sum), .cout(fa_209_cout));
  or or_2 (Error, fa_209_sum, fa_227_sum, fa_244_sum, fa_260_sum, fa_275_sum, fa_289_sum, fa_302_sum, fa_314_sum, fa_325_sum, fa_335_sum, fa_344_sum, fa_352_sum, fa_359_sum, fa_365_sum, fa_370_sum, fa_374_sum, fa_377_sum, fa_379_sum, fa_380_sum, fa_380_cout);
  and and_230 (and_230_out, A[19], B[2]);
  FA fa_210 (.a(fa_191_cout), .b(and_230_out), .cin(fa_192_cout), .sum(fa_210_sum), .cout(fa_210_cout));
  and and_231 (and_231_out, A[18], B[3]);
  FA fa_211 (.a(fa_210_sum), .b(and_231_out), .cin(fa_193_cout), .sum(fa_211_sum), .cout(fa_211_cout));
  and and_232 (and_232_out, A[17], B[4]);
  FA fa_212 (.a(fa_211_sum), .b(and_232_out), .cin(fa_194_cout), .sum(fa_212_sum), .cout(fa_212_cout));
  and and_233 (and_233_out, A[16], B[5]);
  FA fa_213 (.a(fa_212_sum), .b(and_233_out), .cin(fa_195_cout), .sum(fa_213_sum), .cout(fa_213_cout));
  and and_234 (and_234_out, A[15], B[6]);
  FA fa_214 (.a(fa_213_sum), .b(and_234_out), .cin(fa_196_cout), .sum(fa_214_sum), .cout(fa_214_cout));
  and and_235 (and_235_out, A[14], B[7]);
  FA fa_215 (.a(fa_214_sum), .b(and_235_out), .cin(fa_197_cout), .sum(fa_215_sum), .cout(fa_215_cout));
  and and_236 (and_236_out, A[13], B[8]);
  FA fa_216 (.a(fa_215_sum), .b(and_236_out), .cin(fa_198_cout), .sum(fa_216_sum), .cout(fa_216_cout));
  and and_237 (and_237_out, A[12], B[9]);
  FA fa_217 (.a(fa_216_sum), .b(and_237_out), .cin(fa_199_cout), .sum(fa_217_sum), .cout(fa_217_cout));
  and and_238 (and_238_out, A[11], B[10]);
  FA fa_218 (.a(fa_217_sum), .b(and_238_out), .cin(fa_200_cout), .sum(fa_218_sum), .cout(fa_218_cout));
  and and_239 (and_239_out, A[10], B[11]);
  FA fa_219 (.a(fa_218_sum), .b(and_239_out), .cin(fa_201_cout), .sum(fa_219_sum), .cout(fa_219_cout));
  and and_240 (and_240_out, A[9], B[12]);
  FA fa_220 (.a(fa_219_sum), .b(and_240_out), .cin(fa_202_cout), .sum(fa_220_sum), .cout(fa_220_cout));
  and and_241 (and_241_out, A[8], B[13]);
  FA fa_221 (.a(fa_220_sum), .b(and_241_out), .cin(fa_203_cout), .sum(fa_221_sum), .cout(fa_221_cout));
  and and_242 (and_242_out, A[7], B[14]);
  FA fa_222 (.a(fa_221_sum), .b(and_242_out), .cin(fa_204_cout), .sum(fa_222_sum), .cout(fa_222_cout));
  and and_243 (and_243_out, A[6], B[15]);
  FA fa_223 (.a(fa_222_sum), .b(and_243_out), .cin(fa_205_cout), .sum(fa_223_sum), .cout(fa_223_cout));
  and and_244 (and_244_out, A[5], B[16]);
  FA fa_224 (.a(fa_223_sum), .b(and_244_out), .cin(fa_206_cout), .sum(fa_224_sum), .cout(fa_224_cout));
  and and_245 (and_245_out, A[4], B[17]);
  FA fa_225 (.a(fa_224_sum), .b(and_245_out), .cin(fa_207_cout), .sum(fa_225_sum), .cout(fa_225_cout));
  and and_246 (and_246_out, A[3], B[18]);
  FA fa_226 (.a(fa_225_sum), .b(and_246_out), .cin(fa_208_cout), .sum(fa_226_sum), .cout(fa_226_cout));
  and and_247 (and_247_out, A[2], B[19]);
  FA fa_227 (.a(fa_226_sum), .b(and_247_out), .cin(fa_209_cout), .sum(fa_227_sum), .cout(fa_227_cout));
  and and_248 (and_248_out, A[19], B[3]);
  FA fa_228 (.a(fa_210_cout), .b(and_248_out), .cin(fa_211_cout), .sum(fa_228_sum), .cout(fa_228_cout));
  and and_249 (and_249_out, A[18], B[4]);
  FA fa_229 (.a(fa_228_sum), .b(and_249_out), .cin(fa_212_cout), .sum(fa_229_sum), .cout(fa_229_cout));
  and and_250 (and_250_out, A[17], B[5]);
  FA fa_230 (.a(fa_229_sum), .b(and_250_out), .cin(fa_213_cout), .sum(fa_230_sum), .cout(fa_230_cout));
  and and_251 (and_251_out, A[16], B[6]);
  FA fa_231 (.a(fa_230_sum), .b(and_251_out), .cin(fa_214_cout), .sum(fa_231_sum), .cout(fa_231_cout));
  and and_252 (and_252_out, A[15], B[7]);
  FA fa_232 (.a(fa_231_sum), .b(and_252_out), .cin(fa_215_cout), .sum(fa_232_sum), .cout(fa_232_cout));
  and and_253 (and_253_out, A[14], B[8]);
  FA fa_233 (.a(fa_232_sum), .b(and_253_out), .cin(fa_216_cout), .sum(fa_233_sum), .cout(fa_233_cout));
  and and_254 (and_254_out, A[13], B[9]);
  FA fa_234 (.a(fa_233_sum), .b(and_254_out), .cin(fa_217_cout), .sum(fa_234_sum), .cout(fa_234_cout));
  and and_255 (and_255_out, A[12], B[10]);
  FA fa_235 (.a(fa_234_sum), .b(and_255_out), .cin(fa_218_cout), .sum(fa_235_sum), .cout(fa_235_cout));
  and and_256 (and_256_out, A[11], B[11]);
  FA fa_236 (.a(fa_235_sum), .b(and_256_out), .cin(fa_219_cout), .sum(fa_236_sum), .cout(fa_236_cout));
  and and_257 (and_257_out, A[10], B[12]);
  FA fa_237 (.a(fa_236_sum), .b(and_257_out), .cin(fa_220_cout), .sum(fa_237_sum), .cout(fa_237_cout));
  and and_258 (and_258_out, A[9], B[13]);
  FA fa_238 (.a(fa_237_sum), .b(and_258_out), .cin(fa_221_cout), .sum(fa_238_sum), .cout(fa_238_cout));
  and and_259 (and_259_out, A[8], B[14]);
  FA fa_239 (.a(fa_238_sum), .b(and_259_out), .cin(fa_222_cout), .sum(fa_239_sum), .cout(fa_239_cout));
  and and_260 (and_260_out, A[7], B[15]);
  FA fa_240 (.a(fa_239_sum), .b(and_260_out), .cin(fa_223_cout), .sum(fa_240_sum), .cout(fa_240_cout));
  and and_261 (and_261_out, A[6], B[16]);
  FA fa_241 (.a(fa_240_sum), .b(and_261_out), .cin(fa_224_cout), .sum(fa_241_sum), .cout(fa_241_cout));
  and and_262 (and_262_out, A[5], B[17]);
  FA fa_242 (.a(fa_241_sum), .b(and_262_out), .cin(fa_225_cout), .sum(fa_242_sum), .cout(fa_242_cout));
  and and_263 (and_263_out, A[4], B[18]);
  FA fa_243 (.a(fa_242_sum), .b(and_263_out), .cin(fa_226_cout), .sum(fa_243_sum), .cout(fa_243_cout));
  and and_264 (and_264_out, A[3], B[19]);
  FA fa_244 (.a(fa_243_sum), .b(and_264_out), .cin(fa_227_cout), .sum(fa_244_sum), .cout(fa_244_cout));
  and and_265 (and_265_out, A[19], B[4]);
  FA fa_245 (.a(fa_228_cout), .b(and_265_out), .cin(fa_229_cout), .sum(fa_245_sum), .cout(fa_245_cout));
  and and_266 (and_266_out, A[18], B[5]);
  FA fa_246 (.a(fa_245_sum), .b(and_266_out), .cin(fa_230_cout), .sum(fa_246_sum), .cout(fa_246_cout));
  and and_267 (and_267_out, A[17], B[6]);
  FA fa_247 (.a(fa_246_sum), .b(and_267_out), .cin(fa_231_cout), .sum(fa_247_sum), .cout(fa_247_cout));
  and and_268 (and_268_out, A[16], B[7]);
  FA fa_248 (.a(fa_247_sum), .b(and_268_out), .cin(fa_232_cout), .sum(fa_248_sum), .cout(fa_248_cout));
  and and_269 (and_269_out, A[15], B[8]);
  FA fa_249 (.a(fa_248_sum), .b(and_269_out), .cin(fa_233_cout), .sum(fa_249_sum), .cout(fa_249_cout));
  and and_270 (and_270_out, A[14], B[9]);
  FA fa_250 (.a(fa_249_sum), .b(and_270_out), .cin(fa_234_cout), .sum(fa_250_sum), .cout(fa_250_cout));
  and and_271 (and_271_out, A[13], B[10]);
  FA fa_251 (.a(fa_250_sum), .b(and_271_out), .cin(fa_235_cout), .sum(fa_251_sum), .cout(fa_251_cout));
  and and_272 (and_272_out, A[12], B[11]);
  FA fa_252 (.a(fa_251_sum), .b(and_272_out), .cin(fa_236_cout), .sum(fa_252_sum), .cout(fa_252_cout));
  and and_273 (and_273_out, A[11], B[12]);
  FA fa_253 (.a(fa_252_sum), .b(and_273_out), .cin(fa_237_cout), .sum(fa_253_sum), .cout(fa_253_cout));
  and and_274 (and_274_out, A[10], B[13]);
  FA fa_254 (.a(fa_253_sum), .b(and_274_out), .cin(fa_238_cout), .sum(fa_254_sum), .cout(fa_254_cout));
  and and_275 (and_275_out, A[9], B[14]);
  FA fa_255 (.a(fa_254_sum), .b(and_275_out), .cin(fa_239_cout), .sum(fa_255_sum), .cout(fa_255_cout));
  and and_276 (and_276_out, A[8], B[15]);
  FA fa_256 (.a(fa_255_sum), .b(and_276_out), .cin(fa_240_cout), .sum(fa_256_sum), .cout(fa_256_cout));
  and and_277 (and_277_out, A[7], B[16]);
  FA fa_257 (.a(fa_256_sum), .b(and_277_out), .cin(fa_241_cout), .sum(fa_257_sum), .cout(fa_257_cout));
  and and_278 (and_278_out, A[6], B[17]);
  FA fa_258 (.a(fa_257_sum), .b(and_278_out), .cin(fa_242_cout), .sum(fa_258_sum), .cout(fa_258_cout));
  and and_279 (and_279_out, A[5], B[18]);
  FA fa_259 (.a(fa_258_sum), .b(and_279_out), .cin(fa_243_cout), .sum(fa_259_sum), .cout(fa_259_cout));
  and and_280 (and_280_out, A[4], B[19]);
  FA fa_260 (.a(fa_259_sum), .b(and_280_out), .cin(fa_244_cout), .sum(fa_260_sum), .cout(fa_260_cout));
  and and_281 (and_281_out, A[19], B[5]);
  FA fa_261 (.a(fa_245_cout), .b(and_281_out), .cin(fa_246_cout), .sum(fa_261_sum), .cout(fa_261_cout));
  and and_282 (and_282_out, A[18], B[6]);
  FA fa_262 (.a(fa_261_sum), .b(and_282_out), .cin(fa_247_cout), .sum(fa_262_sum), .cout(fa_262_cout));
  and and_283 (and_283_out, A[17], B[7]);
  FA fa_263 (.a(fa_262_sum), .b(and_283_out), .cin(fa_248_cout), .sum(fa_263_sum), .cout(fa_263_cout));
  and and_284 (and_284_out, A[16], B[8]);
  FA fa_264 (.a(fa_263_sum), .b(and_284_out), .cin(fa_249_cout), .sum(fa_264_sum), .cout(fa_264_cout));
  and and_285 (and_285_out, A[15], B[9]);
  FA fa_265 (.a(fa_264_sum), .b(and_285_out), .cin(fa_250_cout), .sum(fa_265_sum), .cout(fa_265_cout));
  and and_286 (and_286_out, A[14], B[10]);
  FA fa_266 (.a(fa_265_sum), .b(and_286_out), .cin(fa_251_cout), .sum(fa_266_sum), .cout(fa_266_cout));
  and and_287 (and_287_out, A[13], B[11]);
  FA fa_267 (.a(fa_266_sum), .b(and_287_out), .cin(fa_252_cout), .sum(fa_267_sum), .cout(fa_267_cout));
  and and_288 (and_288_out, A[12], B[12]);
  FA fa_268 (.a(fa_267_sum), .b(and_288_out), .cin(fa_253_cout), .sum(fa_268_sum), .cout(fa_268_cout));
  and and_289 (and_289_out, A[11], B[13]);
  FA fa_269 (.a(fa_268_sum), .b(and_289_out), .cin(fa_254_cout), .sum(fa_269_sum), .cout(fa_269_cout));
  and and_290 (and_290_out, A[10], B[14]);
  FA fa_270 (.a(fa_269_sum), .b(and_290_out), .cin(fa_255_cout), .sum(fa_270_sum), .cout(fa_270_cout));
  and and_291 (and_291_out, A[9], B[15]);
  FA fa_271 (.a(fa_270_sum), .b(and_291_out), .cin(fa_256_cout), .sum(fa_271_sum), .cout(fa_271_cout));
  and and_292 (and_292_out, A[8], B[16]);
  FA fa_272 (.a(fa_271_sum), .b(and_292_out), .cin(fa_257_cout), .sum(fa_272_sum), .cout(fa_272_cout));
  and and_293 (and_293_out, A[7], B[17]);
  FA fa_273 (.a(fa_272_sum), .b(and_293_out), .cin(fa_258_cout), .sum(fa_273_sum), .cout(fa_273_cout));
  and and_294 (and_294_out, A[6], B[18]);
  FA fa_274 (.a(fa_273_sum), .b(and_294_out), .cin(fa_259_cout), .sum(fa_274_sum), .cout(fa_274_cout));
  and and_295 (and_295_out, A[5], B[19]);
  FA fa_275 (.a(fa_274_sum), .b(and_295_out), .cin(fa_260_cout), .sum(fa_275_sum), .cout(fa_275_cout));
  and and_296 (and_296_out, A[19], B[6]);
  FA fa_276 (.a(fa_261_cout), .b(and_296_out), .cin(fa_262_cout), .sum(fa_276_sum), .cout(fa_276_cout));
  and and_297 (and_297_out, A[18], B[7]);
  FA fa_277 (.a(fa_276_sum), .b(and_297_out), .cin(fa_263_cout), .sum(fa_277_sum), .cout(fa_277_cout));
  and and_298 (and_298_out, A[17], B[8]);
  FA fa_278 (.a(fa_277_sum), .b(and_298_out), .cin(fa_264_cout), .sum(fa_278_sum), .cout(fa_278_cout));
  and and_299 (and_299_out, A[16], B[9]);
  FA fa_279 (.a(fa_278_sum), .b(and_299_out), .cin(fa_265_cout), .sum(fa_279_sum), .cout(fa_279_cout));
  and and_300 (and_300_out, A[15], B[10]);
  FA fa_280 (.a(fa_279_sum), .b(and_300_out), .cin(fa_266_cout), .sum(fa_280_sum), .cout(fa_280_cout));
  and and_301 (and_301_out, A[14], B[11]);
  FA fa_281 (.a(fa_280_sum), .b(and_301_out), .cin(fa_267_cout), .sum(fa_281_sum), .cout(fa_281_cout));
  and and_302 (and_302_out, A[13], B[12]);
  FA fa_282 (.a(fa_281_sum), .b(and_302_out), .cin(fa_268_cout), .sum(fa_282_sum), .cout(fa_282_cout));
  and and_303 (and_303_out, A[12], B[13]);
  FA fa_283 (.a(fa_282_sum), .b(and_303_out), .cin(fa_269_cout), .sum(fa_283_sum), .cout(fa_283_cout));
  and and_304 (and_304_out, A[11], B[14]);
  FA fa_284 (.a(fa_283_sum), .b(and_304_out), .cin(fa_270_cout), .sum(fa_284_sum), .cout(fa_284_cout));
  and and_305 (and_305_out, A[10], B[15]);
  FA fa_285 (.a(fa_284_sum), .b(and_305_out), .cin(fa_271_cout), .sum(fa_285_sum), .cout(fa_285_cout));
  and and_306 (and_306_out, A[9], B[16]);
  FA fa_286 (.a(fa_285_sum), .b(and_306_out), .cin(fa_272_cout), .sum(fa_286_sum), .cout(fa_286_cout));
  and and_307 (and_307_out, A[8], B[17]);
  FA fa_287 (.a(fa_286_sum), .b(and_307_out), .cin(fa_273_cout), .sum(fa_287_sum), .cout(fa_287_cout));
  and and_308 (and_308_out, A[7], B[18]);
  FA fa_288 (.a(fa_287_sum), .b(and_308_out), .cin(fa_274_cout), .sum(fa_288_sum), .cout(fa_288_cout));
  and and_309 (and_309_out, A[6], B[19]);
  FA fa_289 (.a(fa_288_sum), .b(and_309_out), .cin(fa_275_cout), .sum(fa_289_sum), .cout(fa_289_cout));
  and and_310 (and_310_out, A[19], B[7]);
  FA fa_290 (.a(fa_276_cout), .b(and_310_out), .cin(fa_277_cout), .sum(fa_290_sum), .cout(fa_290_cout));
  and and_311 (and_311_out, A[18], B[8]);
  FA fa_291 (.a(fa_290_sum), .b(and_311_out), .cin(fa_278_cout), .sum(fa_291_sum), .cout(fa_291_cout));
  and and_312 (and_312_out, A[17], B[9]);
  FA fa_292 (.a(fa_291_sum), .b(and_312_out), .cin(fa_279_cout), .sum(fa_292_sum), .cout(fa_292_cout));
  and and_313 (and_313_out, A[16], B[10]);
  FA fa_293 (.a(fa_292_sum), .b(and_313_out), .cin(fa_280_cout), .sum(fa_293_sum), .cout(fa_293_cout));
  and and_314 (and_314_out, A[15], B[11]);
  FA fa_294 (.a(fa_293_sum), .b(and_314_out), .cin(fa_281_cout), .sum(fa_294_sum), .cout(fa_294_cout));
  and and_315 (and_315_out, A[14], B[12]);
  FA fa_295 (.a(fa_294_sum), .b(and_315_out), .cin(fa_282_cout), .sum(fa_295_sum), .cout(fa_295_cout));
  and and_316 (and_316_out, A[13], B[13]);
  FA fa_296 (.a(fa_295_sum), .b(and_316_out), .cin(fa_283_cout), .sum(fa_296_sum), .cout(fa_296_cout));
  and and_317 (and_317_out, A[12], B[14]);
  FA fa_297 (.a(fa_296_sum), .b(and_317_out), .cin(fa_284_cout), .sum(fa_297_sum), .cout(fa_297_cout));
  and and_318 (and_318_out, A[11], B[15]);
  FA fa_298 (.a(fa_297_sum), .b(and_318_out), .cin(fa_285_cout), .sum(fa_298_sum), .cout(fa_298_cout));
  and and_319 (and_319_out, A[10], B[16]);
  FA fa_299 (.a(fa_298_sum), .b(and_319_out), .cin(fa_286_cout), .sum(fa_299_sum), .cout(fa_299_cout));
  and and_320 (and_320_out, A[9], B[17]);
  FA fa_300 (.a(fa_299_sum), .b(and_320_out), .cin(fa_287_cout), .sum(fa_300_sum), .cout(fa_300_cout));
  and and_321 (and_321_out, A[8], B[18]);
  FA fa_301 (.a(fa_300_sum), .b(and_321_out), .cin(fa_288_cout), .sum(fa_301_sum), .cout(fa_301_cout));
  and and_322 (and_322_out, A[7], B[19]);
  FA fa_302 (.a(fa_301_sum), .b(and_322_out), .cin(fa_289_cout), .sum(fa_302_sum), .cout(fa_302_cout));
  and and_323 (and_323_out, A[19], B[8]);
  FA fa_303 (.a(fa_290_cout), .b(and_323_out), .cin(fa_291_cout), .sum(fa_303_sum), .cout(fa_303_cout));
  and and_324 (and_324_out, A[18], B[9]);
  FA fa_304 (.a(fa_303_sum), .b(and_324_out), .cin(fa_292_cout), .sum(fa_304_sum), .cout(fa_304_cout));
  and and_325 (and_325_out, A[17], B[10]);
  FA fa_305 (.a(fa_304_sum), .b(and_325_out), .cin(fa_293_cout), .sum(fa_305_sum), .cout(fa_305_cout));
  and and_326 (and_326_out, A[16], B[11]);
  FA fa_306 (.a(fa_305_sum), .b(and_326_out), .cin(fa_294_cout), .sum(fa_306_sum), .cout(fa_306_cout));
  and and_327 (and_327_out, A[15], B[12]);
  FA fa_307 (.a(fa_306_sum), .b(and_327_out), .cin(fa_295_cout), .sum(fa_307_sum), .cout(fa_307_cout));
  and and_328 (and_328_out, A[14], B[13]);
  FA fa_308 (.a(fa_307_sum), .b(and_328_out), .cin(fa_296_cout), .sum(fa_308_sum), .cout(fa_308_cout));
  and and_329 (and_329_out, A[13], B[14]);
  FA fa_309 (.a(fa_308_sum), .b(and_329_out), .cin(fa_297_cout), .sum(fa_309_sum), .cout(fa_309_cout));
  and and_330 (and_330_out, A[12], B[15]);
  FA fa_310 (.a(fa_309_sum), .b(and_330_out), .cin(fa_298_cout), .sum(fa_310_sum), .cout(fa_310_cout));
  and and_331 (and_331_out, A[11], B[16]);
  FA fa_311 (.a(fa_310_sum), .b(and_331_out), .cin(fa_299_cout), .sum(fa_311_sum), .cout(fa_311_cout));
  and and_332 (and_332_out, A[10], B[17]);
  FA fa_312 (.a(fa_311_sum), .b(and_332_out), .cin(fa_300_cout), .sum(fa_312_sum), .cout(fa_312_cout));
  and and_333 (and_333_out, A[9], B[18]);
  FA fa_313 (.a(fa_312_sum), .b(and_333_out), .cin(fa_301_cout), .sum(fa_313_sum), .cout(fa_313_cout));
  and and_334 (and_334_out, A[8], B[19]);
  FA fa_314 (.a(fa_313_sum), .b(and_334_out), .cin(fa_302_cout), .sum(fa_314_sum), .cout(fa_314_cout));
  and and_335 (and_335_out, A[19], B[9]);
  FA fa_315 (.a(fa_303_cout), .b(and_335_out), .cin(fa_304_cout), .sum(fa_315_sum), .cout(fa_315_cout));
  and and_336 (and_336_out, A[18], B[10]);
  FA fa_316 (.a(fa_315_sum), .b(and_336_out), .cin(fa_305_cout), .sum(fa_316_sum), .cout(fa_316_cout));
  and and_337 (and_337_out, A[17], B[11]);
  FA fa_317 (.a(fa_316_sum), .b(and_337_out), .cin(fa_306_cout), .sum(fa_317_sum), .cout(fa_317_cout));
  and and_338 (and_338_out, A[16], B[12]);
  FA fa_318 (.a(fa_317_sum), .b(and_338_out), .cin(fa_307_cout), .sum(fa_318_sum), .cout(fa_318_cout));
  and and_339 (and_339_out, A[15], B[13]);
  FA fa_319 (.a(fa_318_sum), .b(and_339_out), .cin(fa_308_cout), .sum(fa_319_sum), .cout(fa_319_cout));
  and and_340 (and_340_out, A[14], B[14]);
  FA fa_320 (.a(fa_319_sum), .b(and_340_out), .cin(fa_309_cout), .sum(fa_320_sum), .cout(fa_320_cout));
  and and_341 (and_341_out, A[13], B[15]);
  FA fa_321 (.a(fa_320_sum), .b(and_341_out), .cin(fa_310_cout), .sum(fa_321_sum), .cout(fa_321_cout));
  and and_342 (and_342_out, A[12], B[16]);
  FA fa_322 (.a(fa_321_sum), .b(and_342_out), .cin(fa_311_cout), .sum(fa_322_sum), .cout(fa_322_cout));
  and and_343 (and_343_out, A[11], B[17]);
  FA fa_323 (.a(fa_322_sum), .b(and_343_out), .cin(fa_312_cout), .sum(fa_323_sum), .cout(fa_323_cout));
  and and_344 (and_344_out, A[10], B[18]);
  FA fa_324 (.a(fa_323_sum), .b(and_344_out), .cin(fa_313_cout), .sum(fa_324_sum), .cout(fa_324_cout));
  and and_345 (and_345_out, A[9], B[19]);
  FA fa_325 (.a(fa_324_sum), .b(and_345_out), .cin(fa_314_cout), .sum(fa_325_sum), .cout(fa_325_cout));
  and and_346 (and_346_out, A[19], B[10]);
  FA fa_326 (.a(fa_315_cout), .b(and_346_out), .cin(fa_316_cout), .sum(fa_326_sum), .cout(fa_326_cout));
  and and_347 (and_347_out, A[18], B[11]);
  FA fa_327 (.a(fa_326_sum), .b(and_347_out), .cin(fa_317_cout), .sum(fa_327_sum), .cout(fa_327_cout));
  and and_348 (and_348_out, A[17], B[12]);
  FA fa_328 (.a(fa_327_sum), .b(and_348_out), .cin(fa_318_cout), .sum(fa_328_sum), .cout(fa_328_cout));
  and and_349 (and_349_out, A[16], B[13]);
  FA fa_329 (.a(fa_328_sum), .b(and_349_out), .cin(fa_319_cout), .sum(fa_329_sum), .cout(fa_329_cout));
  and and_350 (and_350_out, A[15], B[14]);
  FA fa_330 (.a(fa_329_sum), .b(and_350_out), .cin(fa_320_cout), .sum(fa_330_sum), .cout(fa_330_cout));
  and and_351 (and_351_out, A[14], B[15]);
  FA fa_331 (.a(fa_330_sum), .b(and_351_out), .cin(fa_321_cout), .sum(fa_331_sum), .cout(fa_331_cout));
  and and_352 (and_352_out, A[13], B[16]);
  FA fa_332 (.a(fa_331_sum), .b(and_352_out), .cin(fa_322_cout), .sum(fa_332_sum), .cout(fa_332_cout));
  and and_353 (and_353_out, A[12], B[17]);
  FA fa_333 (.a(fa_332_sum), .b(and_353_out), .cin(fa_323_cout), .sum(fa_333_sum), .cout(fa_333_cout));
  and and_354 (and_354_out, A[11], B[18]);
  FA fa_334 (.a(fa_333_sum), .b(and_354_out), .cin(fa_324_cout), .sum(fa_334_sum), .cout(fa_334_cout));
  and and_355 (and_355_out, A[10], B[19]);
  FA fa_335 (.a(fa_334_sum), .b(and_355_out), .cin(fa_325_cout), .sum(fa_335_sum), .cout(fa_335_cout));
  and and_356 (and_356_out, A[19], B[11]);
  FA fa_336 (.a(fa_326_cout), .b(and_356_out), .cin(fa_327_cout), .sum(fa_336_sum), .cout(fa_336_cout));
  and and_357 (and_357_out, A[18], B[12]);
  FA fa_337 (.a(fa_336_sum), .b(and_357_out), .cin(fa_328_cout), .sum(fa_337_sum), .cout(fa_337_cout));
  and and_358 (and_358_out, A[17], B[13]);
  FA fa_338 (.a(fa_337_sum), .b(and_358_out), .cin(fa_329_cout), .sum(fa_338_sum), .cout(fa_338_cout));
  and and_359 (and_359_out, A[16], B[14]);
  FA fa_339 (.a(fa_338_sum), .b(and_359_out), .cin(fa_330_cout), .sum(fa_339_sum), .cout(fa_339_cout));
  and and_360 (and_360_out, A[15], B[15]);
  FA fa_340 (.a(fa_339_sum), .b(and_360_out), .cin(fa_331_cout), .sum(fa_340_sum), .cout(fa_340_cout));
  and and_361 (and_361_out, A[14], B[16]);
  FA fa_341 (.a(fa_340_sum), .b(and_361_out), .cin(fa_332_cout), .sum(fa_341_sum), .cout(fa_341_cout));
  and and_362 (and_362_out, A[13], B[17]);
  FA fa_342 (.a(fa_341_sum), .b(and_362_out), .cin(fa_333_cout), .sum(fa_342_sum), .cout(fa_342_cout));
  and and_363 (and_363_out, A[12], B[18]);
  FA fa_343 (.a(fa_342_sum), .b(and_363_out), .cin(fa_334_cout), .sum(fa_343_sum), .cout(fa_343_cout));
  and and_364 (and_364_out, A[11], B[19]);
  FA fa_344 (.a(fa_343_sum), .b(and_364_out), .cin(fa_335_cout), .sum(fa_344_sum), .cout(fa_344_cout));
  and and_365 (and_365_out, A[19], B[12]);
  FA fa_345 (.a(fa_336_cout), .b(and_365_out), .cin(fa_337_cout), .sum(fa_345_sum), .cout(fa_345_cout));
  and and_366 (and_366_out, A[18], B[13]);
  FA fa_346 (.a(fa_345_sum), .b(and_366_out), .cin(fa_338_cout), .sum(fa_346_sum), .cout(fa_346_cout));
  and and_367 (and_367_out, A[17], B[14]);
  FA fa_347 (.a(fa_346_sum), .b(and_367_out), .cin(fa_339_cout), .sum(fa_347_sum), .cout(fa_347_cout));
  and and_368 (and_368_out, A[16], B[15]);
  FA fa_348 (.a(fa_347_sum), .b(and_368_out), .cin(fa_340_cout), .sum(fa_348_sum), .cout(fa_348_cout));
  and and_369 (and_369_out, A[15], B[16]);
  FA fa_349 (.a(fa_348_sum), .b(and_369_out), .cin(fa_341_cout), .sum(fa_349_sum), .cout(fa_349_cout));
  and and_370 (and_370_out, A[14], B[17]);
  FA fa_350 (.a(fa_349_sum), .b(and_370_out), .cin(fa_342_cout), .sum(fa_350_sum), .cout(fa_350_cout));
  and and_371 (and_371_out, A[13], B[18]);
  FA fa_351 (.a(fa_350_sum), .b(and_371_out), .cin(fa_343_cout), .sum(fa_351_sum), .cout(fa_351_cout));
  and and_372 (and_372_out, A[12], B[19]);
  FA fa_352 (.a(fa_351_sum), .b(and_372_out), .cin(fa_344_cout), .sum(fa_352_sum), .cout(fa_352_cout));
  and and_373 (and_373_out, A[19], B[13]);
  FA fa_353 (.a(fa_345_cout), .b(and_373_out), .cin(fa_346_cout), .sum(fa_353_sum), .cout(fa_353_cout));
  and and_374 (and_374_out, A[18], B[14]);
  FA fa_354 (.a(fa_353_sum), .b(and_374_out), .cin(fa_347_cout), .sum(fa_354_sum), .cout(fa_354_cout));
  and and_375 (and_375_out, A[17], B[15]);
  FA fa_355 (.a(fa_354_sum), .b(and_375_out), .cin(fa_348_cout), .sum(fa_355_sum), .cout(fa_355_cout));
  and and_376 (and_376_out, A[16], B[16]);
  FA fa_356 (.a(fa_355_sum), .b(and_376_out), .cin(fa_349_cout), .sum(fa_356_sum), .cout(fa_356_cout));
  and and_377 (and_377_out, A[15], B[17]);
  FA fa_357 (.a(fa_356_sum), .b(and_377_out), .cin(fa_350_cout), .sum(fa_357_sum), .cout(fa_357_cout));
  and and_378 (and_378_out, A[14], B[18]);
  FA fa_358 (.a(fa_357_sum), .b(and_378_out), .cin(fa_351_cout), .sum(fa_358_sum), .cout(fa_358_cout));
  and and_379 (and_379_out, A[13], B[19]);
  FA fa_359 (.a(fa_358_sum), .b(and_379_out), .cin(fa_352_cout), .sum(fa_359_sum), .cout(fa_359_cout));
  and and_380 (and_380_out, A[19], B[14]);
  FA fa_360 (.a(fa_353_cout), .b(and_380_out), .cin(fa_354_cout), .sum(fa_360_sum), .cout(fa_360_cout));
  and and_381 (and_381_out, A[18], B[15]);
  FA fa_361 (.a(fa_360_sum), .b(and_381_out), .cin(fa_355_cout), .sum(fa_361_sum), .cout(fa_361_cout));
  and and_382 (and_382_out, A[17], B[16]);
  FA fa_362 (.a(fa_361_sum), .b(and_382_out), .cin(fa_356_cout), .sum(fa_362_sum), .cout(fa_362_cout));
  and and_383 (and_383_out, A[16], B[17]);
  FA fa_363 (.a(fa_362_sum), .b(and_383_out), .cin(fa_357_cout), .sum(fa_363_sum), .cout(fa_363_cout));
  and and_384 (and_384_out, A[15], B[18]);
  FA fa_364 (.a(fa_363_sum), .b(and_384_out), .cin(fa_358_cout), .sum(fa_364_sum), .cout(fa_364_cout));
  and and_385 (and_385_out, A[14], B[19]);
  FA fa_365 (.a(fa_364_sum), .b(and_385_out), .cin(fa_359_cout), .sum(fa_365_sum), .cout(fa_365_cout));
  and and_386 (and_386_out, A[19], B[15]);
  FA fa_366 (.a(fa_360_cout), .b(and_386_out), .cin(fa_361_cout), .sum(fa_366_sum), .cout(fa_366_cout));
  and and_387 (and_387_out, A[18], B[16]);
  FA fa_367 (.a(fa_366_sum), .b(and_387_out), .cin(fa_362_cout), .sum(fa_367_sum), .cout(fa_367_cout));
  and and_388 (and_388_out, A[17], B[17]);
  FA fa_368 (.a(fa_367_sum), .b(and_388_out), .cin(fa_363_cout), .sum(fa_368_sum), .cout(fa_368_cout));
  and and_389 (and_389_out, A[16], B[18]);
  FA fa_369 (.a(fa_368_sum), .b(and_389_out), .cin(fa_364_cout), .sum(fa_369_sum), .cout(fa_369_cout));
  and and_390 (and_390_out, A[15], B[19]);
  FA fa_370 (.a(fa_369_sum), .b(and_390_out), .cin(fa_365_cout), .sum(fa_370_sum), .cout(fa_370_cout));
  and and_391 (and_391_out, A[19], B[16]);
  FA fa_371 (.a(fa_366_cout), .b(and_391_out), .cin(fa_367_cout), .sum(fa_371_sum), .cout(fa_371_cout));
  and and_392 (and_392_out, A[18], B[17]);
  FA fa_372 (.a(fa_371_sum), .b(and_392_out), .cin(fa_368_cout), .sum(fa_372_sum), .cout(fa_372_cout));
  and and_393 (and_393_out, A[17], B[18]);
  FA fa_373 (.a(fa_372_sum), .b(and_393_out), .cin(fa_369_cout), .sum(fa_373_sum), .cout(fa_373_cout));
  and and_394 (and_394_out, A[16], B[19]);
  FA fa_374 (.a(fa_373_sum), .b(and_394_out), .cin(fa_370_cout), .sum(fa_374_sum), .cout(fa_374_cout));
  and and_395 (and_395_out, A[19], B[17]);
  FA fa_375 (.a(fa_371_cout), .b(and_395_out), .cin(fa_372_cout), .sum(fa_375_sum), .cout(fa_375_cout));
  and and_396 (and_396_out, A[18], B[18]);
  FA fa_376 (.a(fa_375_sum), .b(and_396_out), .cin(fa_373_cout), .sum(fa_376_sum), .cout(fa_376_cout));
  and and_397 (and_397_out, A[17], B[19]);
  FA fa_377 (.a(fa_376_sum), .b(and_397_out), .cin(fa_374_cout), .sum(fa_377_sum), .cout(fa_377_cout));
  and and_398 (and_398_out, A[19], B[18]);
  FA fa_378 (.a(fa_375_cout), .b(and_398_out), .cin(fa_376_cout), .sum(fa_378_sum), .cout(fa_378_cout));
  and and_399 (and_399_out, A[18], B[19]);
  FA fa_379 (.a(fa_378_sum), .b(and_399_out), .cin(fa_377_cout), .sum(fa_379_sum), .cout(fa_379_cout));
  and and_400 (and_400_out, A[19], B[19]);
  FA fa_380 (.a(fa_378_cout), .b(and_400_out), .cin(fa_379_cout), .sum(fa_380_sum), .cout(fa_380_cout));
endmodule

module BtoBCD (
  input  [19:0] in_1,
  output [3:0] d0,
  output [3:0] d1,
  output [3:0] d2,
  output [3:0] d3,
  output [3:0] d4,
  output [3:0] d5
);

  wire bcdunit_3_q, bcdunit_5_q, bcdunit_7_q, bcdunit_8_q, bcdunit_10_q, bcdunit_11_q, bcdunit_13_q,
       bcdunit_14_q, bcdunit_15_q, bcdunit_17_q, bcdunit_18_q, bcdunit_19_q, bcdunit_21_q, bcdunit_22_q,
       bcdunit_23_q, bcdunit_24_q, bcdunit_26_q, bcdunit_27_q, bcdunit_28_q, bcdunit_29_q, bcdunit_31_q,
       bcdunit_32_q, bcdunit_33_q, bcdunit_34_q, bcdunit_35_q, bcdunit_37_q, bcdunit_38_q, bcdunit_39_q,
       bcdunit_40_q, bcdunit_41_q, bcdunit_43_q, bcdunit_44_q, bcdunit_45_q, bcdunit_46_q, bcdunit_47_q,
       bcdunit_48_q, bcdunit_49_q, bcdunit_50_q, bcdunit_51_q, bcdunit_52_q, bcdunit_53_q, bcdunit_54_q,
       bcdunit_55_q, bcdunit_56_q, bcdunit_57_q, bcdunit_58_q, bcdunit_59_q, bcdunit_60_q, bcdunit_61_q,
       bcdunit_62_q, bcdunit_63_q;
  wire [1:0] bcdunit_2_q, bcdunit_6_q, bcdunit_12_q, bcdunit_20_q, bcdunit_30_q;
  wire [2:0] bcdunit_1_r2r1r0, bcdunit_2_r2r1r0, bcdunit_3_r2r1r0, bcdunit_4_r2r1r0, bcdunit_5_r2r1r0,
       bcdunit_6_r2r1r0, bcdunit_7_r2r1r0, bcdunit_8_r2r1r0, bcdunit_9_r2r1r0, bcdunit_10_r2r1r0,
       bcdunit_11_r2r1r0, bcdunit_12_r2r1r0, bcdunit_13_r2r1r0, bcdunit_14_r2r1r0, bcdunit_15_r2r1r0,
       bcdunit_16_r2r1r0, bcdunit_17_r2r1r0, bcdunit_18_r2r1r0, bcdunit_19_r2r1r0, bcdunit_20_r2r1r0,
       bcdunit_21_r2r1r0, bcdunit_22_r2r1r0, bcdunit_23_r2r1r0, bcdunit_24_r2r1r0, bcdunit_25_r2r1r0,
       bcdunit_26_r2r1r0, bcdunit_27_r2r1r0, bcdunit_28_r2r1r0, bcdunit_29_r2r1r0, bcdunit_30_r2r1r0,
       bcdunit_31_r2r1r0, bcdunit_32_r2r1r0, bcdunit_33_r2r1r0, bcdunit_34_r2r1r0, bcdunit_35_r2r1r0,
       bcdunit_36_r2r1r0, bcdunit_37_r2r1r0, bcdunit_38_r2r1r0, bcdunit_39_r2r1r0, bcdunit_40_r2r1r0,
       bcdunit_41_r2r1r0, bcdunit_42_r2r1r0, bcdunit_43_r2r1r0, bcdunit_44_r2r1r0, bcdunit_45_r2r1r0,
       bcdunit_46_r2r1r0, bcdunit_47_r2r1r0, bcdunit_48_r2r1r0, bcdunit_49_r2r1r0, bcdunit_50_r2r1r0,
       bcdunit_51_r2r1r0, bcdunit_52_r2r1r0, bcdunit_53_r2r1r0, bcdunit_54_r2r1r0, bcdunit_55_r2r1r0,
       bcdunit_56_r2r1r0, bcdunit_57_r2r1r0, bcdunit_58_r2r1r0, bcdunit_59_r2r1r0, bcdunit_60_r2r1r0,
       bcdunit_61_r2r1r0, bcdunit_62_r2r1r0, bcdunit_63_r2r1r0;

  BCDunit bcdunit_1 (.n(in_1[17]), .c2c1c0({1'b0, in_1[19:18]}), .r2r1r0(bcdunit_1_r2r1r0), .q(bcdunit_2_q[1]));
  BCDunit bcdunit_2 (.n(in_1[16]), .c2c1c0(bcdunit_1_r2r1r0), .r2r1r0(bcdunit_2_r2r1r0), .q(bcdunit_2_q[0]));
  BCDunit bcdunit_3 (.n(in_1[15]), .c2c1c0(bcdunit_2_r2r1r0), .r2r1r0(bcdunit_3_r2r1r0), .q(bcdunit_3_q));
  BCDunit bcdunit_4 (.n(bcdunit_3_q), .c2c1c0({1'b0, bcdunit_2_q}), .r2r1r0(bcdunit_4_r2r1r0), .q(bcdunit_6_q[1]));
  BCDunit bcdunit_5 (.n(in_1[14]), .c2c1c0(bcdunit_3_r2r1r0), .r2r1r0(bcdunit_5_r2r1r0), .q(bcdunit_5_q));
  BCDunit bcdunit_6 (.n(bcdunit_5_q), .c2c1c0(bcdunit_4_r2r1r0), .r2r1r0(bcdunit_6_r2r1r0), .q(bcdunit_6_q[0]));
  BCDunit bcdunit_7 (.n(in_1[13]), .c2c1c0(bcdunit_5_r2r1r0), .r2r1r0(bcdunit_7_r2r1r0), .q(bcdunit_7_q));
  BCDunit bcdunit_8 (.n(bcdunit_7_q), .c2c1c0(bcdunit_6_r2r1r0), .r2r1r0(bcdunit_8_r2r1r0), .q(bcdunit_8_q));
  BCDunit bcdunit_9 (.n(bcdunit_8_q), .c2c1c0({1'b0, bcdunit_6_q}), .r2r1r0(bcdunit_9_r2r1r0), .q(bcdunit_12_q[1]));
  BCDunit bcdunit_10 (.n(in_1[12]), .c2c1c0(bcdunit_7_r2r1r0), .r2r1r0(bcdunit_10_r2r1r0), .q(bcdunit_10_q));
  BCDunit bcdunit_11 (.n(bcdunit_10_q), .c2c1c0(bcdunit_8_r2r1r0), .r2r1r0(bcdunit_11_r2r1r0), .q(bcdunit_11_q));
  BCDunit bcdunit_12 (.n(bcdunit_11_q), .c2c1c0(bcdunit_9_r2r1r0), .r2r1r0(bcdunit_12_r2r1r0), .q(bcdunit_12_q[0]));
  BCDunit bcdunit_13 (.n(in_1[11]), .c2c1c0(bcdunit_10_r2r1r0), .r2r1r0(bcdunit_13_r2r1r0), .q(bcdunit_13_q));
  BCDunit bcdunit_14 (.n(bcdunit_13_q), .c2c1c0(bcdunit_11_r2r1r0), .r2r1r0(bcdunit_14_r2r1r0), .q(bcdunit_14_q));
  BCDunit bcdunit_15 (.n(bcdunit_14_q), .c2c1c0(bcdunit_12_r2r1r0), .r2r1r0(bcdunit_15_r2r1r0), .q(bcdunit_15_q));
  BCDunit bcdunit_16 (.n(bcdunit_15_q), .c2c1c0({1'b0, bcdunit_12_q}), .r2r1r0(bcdunit_16_r2r1r0), .q(bcdunit_20_q[1]));
  BCDunit bcdunit_17 (.n(in_1[10]), .c2c1c0(bcdunit_13_r2r1r0), .r2r1r0(bcdunit_17_r2r1r0), .q(bcdunit_17_q));
  BCDunit bcdunit_18 (.n(bcdunit_17_q), .c2c1c0(bcdunit_14_r2r1r0), .r2r1r0(bcdunit_18_r2r1r0), .q(bcdunit_18_q));
  BCDunit bcdunit_19 (.n(bcdunit_18_q), .c2c1c0(bcdunit_15_r2r1r0), .r2r1r0(bcdunit_19_r2r1r0), .q(bcdunit_19_q));
  BCDunit bcdunit_20 (.n(bcdunit_19_q), .c2c1c0(bcdunit_16_r2r1r0), .r2r1r0(bcdunit_20_r2r1r0), .q(bcdunit_20_q[0]));
  BCDunit bcdunit_21 (.n(in_1[9]), .c2c1c0(bcdunit_17_r2r1r0), .r2r1r0(bcdunit_21_r2r1r0), .q(bcdunit_21_q));
  BCDunit bcdunit_22 (.n(bcdunit_21_q), .c2c1c0(bcdunit_18_r2r1r0), .r2r1r0(bcdunit_22_r2r1r0), .q(bcdunit_22_q));
  BCDunit bcdunit_23 (.n(bcdunit_22_q), .c2c1c0(bcdunit_19_r2r1r0), .r2r1r0(bcdunit_23_r2r1r0), .q(bcdunit_23_q));
  BCDunit bcdunit_24 (.n(bcdunit_23_q), .c2c1c0(bcdunit_20_r2r1r0), .r2r1r0(bcdunit_24_r2r1r0), .q(bcdunit_24_q));
  BCDunit bcdunit_25 (.n(bcdunit_24_q), .c2c1c0({1'b0, bcdunit_20_q}), .r2r1r0(bcdunit_25_r2r1r0), .q(bcdunit_30_q[1]));
  BCDunit bcdunit_26 (.n(in_1[8]), .c2c1c0(bcdunit_21_r2r1r0), .r2r1r0(bcdunit_26_r2r1r0), .q(bcdunit_26_q));
  BCDunit bcdunit_27 (.n(bcdunit_26_q), .c2c1c0(bcdunit_22_r2r1r0), .r2r1r0(bcdunit_27_r2r1r0), .q(bcdunit_27_q));
  BCDunit bcdunit_28 (.n(bcdunit_27_q), .c2c1c0(bcdunit_23_r2r1r0), .r2r1r0(bcdunit_28_r2r1r0), .q(bcdunit_28_q));
  BCDunit bcdunit_29 (.n(bcdunit_28_q), .c2c1c0(bcdunit_24_r2r1r0), .r2r1r0(bcdunit_29_r2r1r0), .q(bcdunit_29_q));
  BCDunit bcdunit_30 (.n(bcdunit_29_q), .c2c1c0(bcdunit_25_r2r1r0), .r2r1r0(bcdunit_30_r2r1r0), .q(bcdunit_30_q[0]));
  BCDunit bcdunit_31 (.n(in_1[7]), .c2c1c0(bcdunit_26_r2r1r0), .r2r1r0(bcdunit_31_r2r1r0), .q(bcdunit_31_q));
  BCDunit bcdunit_32 (.n(bcdunit_31_q), .c2c1c0(bcdunit_27_r2r1r0), .r2r1r0(bcdunit_32_r2r1r0), .q(bcdunit_32_q));
  BCDunit bcdunit_33 (.n(bcdunit_32_q), .c2c1c0(bcdunit_28_r2r1r0), .r2r1r0(bcdunit_33_r2r1r0), .q(bcdunit_33_q));
  BCDunit bcdunit_34 (.n(bcdunit_33_q), .c2c1c0(bcdunit_29_r2r1r0), .r2r1r0(bcdunit_34_r2r1r0), .q(bcdunit_34_q));
  BCDunit bcdunit_35 (.n(bcdunit_34_q), .c2c1c0(bcdunit_30_r2r1r0), .r2r1r0(bcdunit_35_r2r1r0), .q(bcdunit_35_q));
  BCDunit bcdunit_36 (.n(bcdunit_35_q), .c2c1c0({1'b0, bcdunit_30_q}), .r2r1r0(bcdunit_36_r2r1r0));  // open: q
  BCDunit bcdunit_37 (.n(in_1[6]), .c2c1c0(bcdunit_31_r2r1r0), .r2r1r0(bcdunit_37_r2r1r0), .q(bcdunit_37_q));
  BCDunit bcdunit_38 (.n(bcdunit_37_q), .c2c1c0(bcdunit_32_r2r1r0), .r2r1r0(bcdunit_38_r2r1r0), .q(bcdunit_38_q));
  BCDunit bcdunit_39 (.n(bcdunit_38_q), .c2c1c0(bcdunit_33_r2r1r0), .r2r1r0(bcdunit_39_r2r1r0), .q(bcdunit_39_q));
  BCDunit bcdunit_40 (.n(bcdunit_39_q), .c2c1c0(bcdunit_34_r2r1r0), .r2r1r0(bcdunit_40_r2r1r0), .q(bcdunit_40_q));
  BCDunit bcdunit_41 (.n(bcdunit_40_q), .c2c1c0(bcdunit_35_r2r1r0), .r2r1r0(bcdunit_41_r2r1r0), .q(bcdunit_41_q));
  BCDunit bcdunit_42 (.n(bcdunit_41_q), .c2c1c0(bcdunit_36_r2r1r0), .r2r1r0(bcdunit_42_r2r1r0));  // open: q
  BCDunit bcdunit_43 (.n(in_1[5]), .c2c1c0(bcdunit_37_r2r1r0), .r2r1r0(bcdunit_43_r2r1r0), .q(bcdunit_43_q));
  BCDunit bcdunit_44 (.n(bcdunit_43_q), .c2c1c0(bcdunit_38_r2r1r0), .r2r1r0(bcdunit_44_r2r1r0), .q(bcdunit_44_q));
  BCDunit bcdunit_45 (.n(bcdunit_44_q), .c2c1c0(bcdunit_39_r2r1r0), .r2r1r0(bcdunit_45_r2r1r0), .q(bcdunit_45_q));
  BCDunit bcdunit_46 (.n(bcdunit_45_q), .c2c1c0(bcdunit_40_r2r1r0), .r2r1r0(bcdunit_46_r2r1r0), .q(bcdunit_46_q));
  BCDunit bcdunit_47 (.n(bcdunit_46_q), .c2c1c0(bcdunit_41_r2r1r0), .r2r1r0(bcdunit_47_r2r1r0), .q(bcdunit_47_q));
  BCDunit bcdunit_48 (.n(bcdunit_47_q), .c2c1c0(bcdunit_42_r2r1r0), .r2r1r0(bcdunit_48_r2r1r0), .q(bcdunit_48_q));
  BCDunit bcdunit_49 (.n(in_1[4]), .c2c1c0(bcdunit_43_r2r1r0), .r2r1r0(bcdunit_49_r2r1r0), .q(bcdunit_49_q));
  BCDunit bcdunit_50 (.n(bcdunit_49_q), .c2c1c0(bcdunit_44_r2r1r0), .r2r1r0(bcdunit_50_r2r1r0), .q(bcdunit_50_q));
  BCDunit bcdunit_51 (.n(bcdunit_50_q), .c2c1c0(bcdunit_45_r2r1r0), .r2r1r0(bcdunit_51_r2r1r0), .q(bcdunit_51_q));
  BCDunit bcdunit_52 (.n(bcdunit_51_q), .c2c1c0(bcdunit_46_r2r1r0), .r2r1r0(bcdunit_52_r2r1r0), .q(bcdunit_52_q));
  BCDunit bcdunit_53 (.n(bcdunit_52_q), .c2c1c0(bcdunit_47_r2r1r0), .r2r1r0(bcdunit_53_r2r1r0), .q(bcdunit_53_q));
  BCDunit bcdunit_54 (.n(in_1[3]), .c2c1c0(bcdunit_49_r2r1r0), .r2r1r0(bcdunit_54_r2r1r0), .q(bcdunit_54_q));
  BCDunit bcdunit_55 (.n(bcdunit_54_q), .c2c1c0(bcdunit_50_r2r1r0), .r2r1r0(bcdunit_55_r2r1r0), .q(bcdunit_55_q));
  BCDunit bcdunit_56 (.n(bcdunit_55_q), .c2c1c0(bcdunit_51_r2r1r0), .r2r1r0(bcdunit_56_r2r1r0), .q(bcdunit_56_q));
  BCDunit bcdunit_57 (.n(bcdunit_56_q), .c2c1c0(bcdunit_52_r2r1r0), .r2r1r0(bcdunit_57_r2r1r0), .q(bcdunit_57_q));
  BCDunit bcdunit_58 (.n(in_1[2]), .c2c1c0(bcdunit_54_r2r1r0), .r2r1r0(bcdunit_58_r2r1r0), .q(bcdunit_58_q));
  BCDunit bcdunit_59 (.n(bcdunit_58_q), .c2c1c0(bcdunit_55_r2r1r0), .r2r1r0(bcdunit_59_r2r1r0), .q(bcdunit_59_q));
  BCDunit bcdunit_60 (.n(bcdunit_59_q), .c2c1c0(bcdunit_56_r2r1r0), .r2r1r0(bcdunit_60_r2r1r0), .q(bcdunit_60_q));
  BCDunit bcdunit_61 (.n(in_1[1]), .c2c1c0(bcdunit_58_r2r1r0), .r2r1r0(bcdunit_61_r2r1r0), .q(bcdunit_61_q));
  BCDunit bcdunit_62 (.n(bcdunit_61_q), .c2c1c0(bcdunit_59_r2r1r0), .r2r1r0(bcdunit_62_r2r1r0), .q(bcdunit_62_q));
  pp pp_1 (
    .in_1(bcdunit_48_r2r1r0[0]), .in_2(bcdunit_48_r2r1r0[1]), .in_3(bcdunit_48_r2r1r0[2]),
    .in_4(bcdunit_48_q), .out_5(d5));
  BCDunit bcdunit_63 (.n(in_1[0]), .c2c1c0(bcdunit_61_r2r1r0), .r2r1r0(bcdunit_63_r2r1r0), .q(bcdunit_63_q));
  pp pp_2 (
    .in_1(bcdunit_53_r2r1r0[0]), .in_2(bcdunit_53_r2r1r0[1]), .in_3(bcdunit_53_r2r1r0[2]),
    .in_4(bcdunit_53_q), .out_5(d4));
  pp pp_3 (
    .in_1(bcdunit_57_r2r1r0[0]), .in_2(bcdunit_57_r2r1r0[1]), .in_3(bcdunit_57_r2r1r0[2]),
    .in_4(bcdunit_57_q), .out_5(d3));
  pp pp_4 (
    .in_1(bcdunit_60_r2r1r0[0]), .in_2(bcdunit_60_r2r1r0[1]), .in_3(bcdunit_60_r2r1r0[2]),
    .in_4(bcdunit_60_q), .out_5(d2));
  pp pp_5 (
    .in_1(bcdunit_63_r2r1r0[0]), .in_2(bcdunit_63_r2r1r0[1]), .in_3(bcdunit_63_r2r1r0[2]),
    .in_4(bcdunit_63_q), .out_5(d0));
  pp pp_6 (
    .in_1(bcdunit_62_r2r1r0[0]), .in_2(bcdunit_62_r2r1r0[1]), .in_3(bcdunit_62_r2r1r0[2]),
    .in_4(bcdunit_62_q), .out_5(d1));
endmodule

module lastestInputN (
  input  [20:0] in_1,
  input  C,
  input  N,
  input  B,
  output [3:0] out_5,
  output [3:0] out_6,
  output [3:0] out_7,
  output [3:0] out_8,
  output [3:0] out_9,
  output [3:0] out_10
);

  wire and_1_out, clock_1_out, nor_1_out, risingdetector_2_out_2, risingdetector_3_out_2,
       risingdetector_4_out_2, undriven, undriven_2;
  wire [4:0] risingdetector_1_out_2;
  wire [20:0] mux_1_b, mux_2_b, mux_3_b, mux_4_b, mux_5_b, mux_6_b;
  wire [20:4] register_1_q, register_2_q, register_3_q, register_4_q, register_5_q, register_6_q;

  nor nor_1 (nor_1_out, register_6_q[19], register_6_q[18], register_6_q[17], register_6_q[16], register_6_q[15], register_6_q[14], register_6_q[13], register_6_q[12], register_6_q[11], register_6_q[10], register_6_q[20], register_6_q[8], register_6_q[7], register_6_q[6], register_6_q[5], register_6_q[4], out_10[3], out_10[2], out_10[1], out_10[0], register_6_q[9]);
  RisingDetector risingdetector_1 (.in_1(C), .out_2(risingdetector_1_out_2[0]));
  and and_1 (and_1_out, N, nor_1_out);
  RisingDetector risingdetector_2 (.in_1(and_1_out), .out_2(risingdetector_2_out_2));
  RisingDetector risingdetector_3 (.in_1(B), .out_2(risingdetector_3_out_2));
  RisingDetector risingdetector_4 (.in_1(undriven), .out_2(risingdetector_4_out_2));
  and and_2 (risingdetector_1_out_2[1], ~risingdetector_1_out_2[0], risingdetector_2_out_2);  // AND_Gate
  and and_3 (risingdetector_1_out_2[2], ~risingdetector_1_out_2[0], ~risingdetector_2_out_2, risingdetector_3_out_2);  // AND_Gate
  and and_4 (risingdetector_1_out_2[3], ~risingdetector_1_out_2[0], ~risingdetector_2_out_2, ~risingdetector_3_out_2, risingdetector_4_out_2);  // AND_Gate
  nor nor_2 (risingdetector_1_out_2[4], risingdetector_1_out_2[0], risingdetector_1_out_2[1], risingdetector_1_out_2[2], risingdetector_1_out_2[3]);
  mux mux_1 (
    .s(risingdetector_1_out_2), .a4({register_1_q, out_5}), .a2({register_2_q, out_6}), .a1(in_1),
    .a0({21{1'b0}}), .b(mux_1_b));  // open: a3
  mux mux_2 (
    .s(risingdetector_1_out_2), .a4({register_2_q, out_6}), .a2({register_3_q, out_7}),
    .a1({register_1_q, out_5}), .a0({21{1'b0}}), .b(mux_2_b));  // open: a3
  Register #(.width(21)) register_1 (.D(mux_1_b), .clk(clock_1_out), .Q({register_1_q, out_5}));  // open: en, clr
  Register #(.width(21)) register_2 (.D(mux_2_b), .clk(clock_1_out), .Q({register_2_q, out_6}));  // open: en, clr
  Register #(.width(21)) register_3 (.D(mux_3_b), .clk(clock_1_out), .Q({register_3_q, out_7}));  // open: en, clr
  mux mux_3 (
    .s(risingdetector_1_out_2), .a4({register_3_q, out_7}), .a2({register_4_q, out_8}),
    .a1({register_2_q, out_6}), .a0({21{1'b0}}), .b(mux_3_b));  // open: a3
  Register #(.width(21)) register_4 (
    .D(mux_4_b), .clk(clock_1_out), .Q({register_4_q, out_8}), .clr(undriven_2));  // open: en
  mux mux_4 (
    .s(risingdetector_1_out_2), .a4({register_4_q, out_8}), .a2({register_5_q, out_9}),
    .a1({register_3_q, out_7}), .a0({21{1'b0}}), .b(mux_4_b));  // open: a3
  Register #(.width(21)) register_5 (.D(mux_5_b), .clk(clock_1_out), .Q({register_5_q, out_9}));  // open: en, clr
  mux mux_5 (
    .s(risingdetector_1_out_2), .a4({register_5_q, out_9}), .a2({register_6_q, out_10}),
    .a1({register_4_q, out_8}), .a0({21{1'b0}}), .b(mux_5_b));  // open: a3
  Register #(.width(21)) register_6 (.D(mux_6_b), .clk(clock_1_out), .Q({register_6_q, out_10}));  // open: en, clr
  mux mux_6 (
    .s(risingdetector_1_out_2), .a4({register_6_q, out_10}), .a1({register_5_q, out_9}), .a0({21{1'b0}}),
    .b(mux_6_b));  // open: a3, a2
  Clock clock_1 (.out(clock_1_out));
endmodule

module forMux (
  input  in_1,
  input  in_2,
  input  in_3,
  input  in_4,
  output [4:0] out_5
);

  nor nor_1 (out_5[4], in_4, in_3, in_2, in_1);

  assign out_5[3:0] = {in_1, in_2, in_3, in_4};
endmodule

module newstate (
  input  reset,
  input  number,
  input  plus,
  input  minus,
  input  multi,
  input  equal,
  output res,
  output A,
  output Ap,
  output Am,
  output Ax,
  output ApN,
  output AmN,
  output AxN,
  output ApNp,
  output ApNx,
  output ApNm,
  output AmNp,
  output AmNx,
  output AmNm
);

  wire and_1_out, and_2_out, and_3_out, and_4_out, and_5_out, and_6_out, and_7_out, and_8_out, and_9_out,
       and_10_out, and_11_out, and_12_out, and_13_out, and_14_out, and_15_out, and_16_out, and_17_out,
       and_18_out, and_19_out, and_20_out, and_21_out, and_22_out, and_23_out, and_24_out, and_25_out,
       and_26_out, and_27_out, and_28_out, and_29_out, and_30_out, and_31_out, and_32_out, and_33_out,
       and_34_out, and_35_out, and_36_out, and_37_out, and_38_out, and_39_out, and_40_out, and_41_out,
       and_42_out, and_43_out, and_44_out, and_45_out, and_46_out, and_47_out, and_48_out, and_49_out,
       and_50_out, and_51_out, and_52_out, and_53_out, and_54_out, and_55_out, and_56_out, and_57_out,
       and_58_out, and_59_out, and_60_out, and_61_out, and_62_out, and_63_out, and_64_out, and_65_out,
       clock_1_out, clock_2_out, clock_3_out, clock_4_out, clock_5_out, clock_6_out, clock_7_out,
       clock_8_out, clock_9_out, clock_10_out, clock_11_out, clock_12_out, clock_13_out, clock_14_out,
       nor_1_out, nor_2_out, or_1_out, or_2_out, or_3_out, or_4_out, or_5_out, or_6_out, or_7_out, or_8_out,
       or_9_out, or_10_out, or_11_out, or_12_out, or_13_out, or_14_out, or_15_out, or_16_out, or_17_out,
       or_18_out, or_19_out, or_20_out, or_21_out, or_23_out, or_24_out, or_25_out, or_26_out, or_27_out,
       or_28_out, or_29_out;

  nor nor_1 (nor_1_out, reset, equal, multi, minus, plus, number);
  nor nor_2 (nor_2_out, A, Ap, Am, Ax, ApN, AmN, AxN, ApNp, ApNx, ApNm, AmNp, AmNx, AmNm);
  and and_1 (and_1_out, number, res);
  and and_2 (and_2_out, Ap, equal);
  and and_3 (and_3_out, Am, equal);
  and and_4 (and_4_out, Ax, equal);
  and and_5 (and_5_out, ApN, equal);
  and and_6 (and_6_out, AmN, equal);
  and and_7 (and_7_out, AxN, equal);
  and and_8 (and_8_out, ApNp, equal);
  and and_9 (and_9_out, ApNx, equal);
  and and_10 (and_10_out, ApNm, equal);
  and and_11 (and_11_out, AmNp, equal);
  and and_12 (and_12_out, AmNx, equal);
  and and_13 (and_13_out, AmNm, equal);
  and and_14 (and_14_out, plus, A);
  and and_15 (and_15_out, plus, Am);
  and and_16 (and_16_out, plus, Ax);
  and and_17 (and_17_out, plus, ApN);
  and and_18 (and_18_out, plus, AmN);
  and and_19 (and_19_out, plus, AxN);
  and and_20 (and_20_out, minus, A);
  and and_21 (and_21_out, minus, Ap);
  and and_22 (and_22_out, minus, Ax);
  and and_23 (and_23_out, minus, ApN);
  and and_24 (and_24_out, minus, AmN);
  and and_25 (and_25_out, minus, AxN);
  and and_26 (and_26_out, multi, A);
  and and_27 (and_27_out, multi, Ap);
  and and_28 (and_28_out, multi, Am);
  and and_29 (and_29_out, multi, AxN);
  and and_30 (and_30_out, number, Ap);
  and and_31 (and_31_out, number, ApNp);
  and and_32 (and_32_out, number, ApNx);
  and and_33 (and_33_out, number, AmNp);
  and and_34 (and_34_out, number, Am);
  and and_35 (and_35_out, number, ApNm);
  and and_36 (and_36_out, number, AmNx);
  and and_37 (and_37_out, number, AmNm);
  and and_38 (and_38_out, number, Ax);
  and and_39 (and_39_out, plus, ApNx);
  and and_40 (and_40_out, plus, ApNm);
  and and_41 (and_41_out, multi, ApN);
  and and_42 (and_42_out, multi, ApNp);
  and and_43 (and_43_out, multi, ApNm);
  and and_44 (and_44_out, minus, ApNp);
  and and_45 (and_45_out, minus, ApNx);
  and and_46 (and_46_out, plus, AmNx);
  and and_47 (and_47_out, plus, AmNm);
  and and_48 (and_48_out, multi, AmN);
  and and_49 (and_49_out, multi, AmNp);
  and and_50 (and_50_out, multi, AmNm);
  and and_51 (and_51_out, minus, AmNp);
  and and_52 (and_52_out, minus, AmNx);
  or or_1 (or_1_out, number, nor_1_out);
  and and_53 (and_53_out, or_1_out, A);
  and and_54 (and_54_out, ApNp, or_2_out);
  or or_2 (or_2_out, plus, nor_1_out);
  or or_3 (or_3_out, minus, nor_1_out);
  or or_4 (or_4_out, nor_1_out, minus);
  or or_5 (or_5_out, plus, nor_1_out);
  and and_55 (and_55_out, Ap, or_5_out);
  and and_56 (and_56_out, Am, or_6_out);
  or or_6 (or_6_out, minus, nor_1_out);
  and and_57 (and_57_out, Ax, or_7_out);
  or or_7 (or_7_out, multi, nor_1_out);
  and and_58 (and_58_out, ApN, or_8_out);
  or or_8 (or_8_out, number, nor_1_out);
  and and_59 (and_59_out, AmN, or_9_out);
  or or_9 (or_9_out, number, nor_1_out);
  and and_60 (and_60_out, AxN, or_17_out);
  and and_61 (and_61_out, ApNx, or_20_out);
  and and_62 (and_62_out, ApNm, or_3_out);
  and and_63 (and_63_out, AmNp, or_24_out);
  and and_64 (and_64_out, AmNx, or_26_out);
  and and_65 (and_65_out, AmNm, or_4_out);
  or or_10 (or_10_out, reset, nor_2_out);
  or or_11 (or_11_out, and_53_out, and_1_out, and_2_out, and_3_out, and_4_out, and_5_out, and_6_out, and_7_out, and_8_out, and_9_out, and_10_out, and_11_out, and_12_out, and_13_out);
  or or_12 (or_12_out, and_55_out, and_14_out, and_15_out, and_16_out, and_17_out, and_18_out, and_19_out);
  or or_13 (or_13_out, and_56_out, and_20_out, and_21_out, and_22_out, and_23_out, and_24_out, and_25_out);
  or or_14 (or_14_out, and_57_out, and_26_out, and_27_out, and_28_out, and_29_out);
  or or_15 (or_15_out, and_58_out, and_30_out, and_31_out, and_32_out, and_33_out);
  or or_16 (or_16_out, and_59_out, and_34_out, and_35_out, and_36_out, and_37_out);
  or or_17 (or_17_out, number, nor_1_out);
  or or_18 (or_18_out, and_38_out, and_60_out);
  or or_19 (or_19_out, and_39_out, and_40_out, and_54_out);
  or or_20 (or_20_out, multi, nor_1_out);
  or or_21 (or_21_out, and_41_out, and_42_out, and_43_out, and_61_out);
  // OR_Gate or_22 is placed but not wired
  or or_23 (or_23_out, and_44_out, and_45_out, and_62_out);
  or or_24 (or_24_out, plus, nor_1_out);
  or or_25 (or_25_out, and_46_out, and_47_out, and_63_out);
  or or_26 (or_26_out, nor_1_out, multi);
  or or_27 (or_27_out, and_48_out, and_49_out, and_50_out, and_64_out);
  or or_28 (or_28_out, and_51_out, and_52_out, and_65_out);
  or or_29 (or_29_out, equal, or_11_out);
  D_Flip_Flop R (.D(or_10_out), .clk(clock_1_out), .Q(res));  // open: Qn, preset, reset
  Clock clock_1 (.out(clock_1_out));
  D_Flip_Flop d_ff_1 (.D(or_29_out), .clk(clock_2_out), .Q(A));  // open: Qn, preset, reset
  Clock clock_2 (.out(clock_2_out));
  D_Flip_Flop d_ff_2 (.D(or_12_out), .clk(clock_3_out), .Q(Ap));  // open: Qn, preset, reset
  Clock clock_3 (.out(clock_3_out));
  D_Flip_Flop d_ff_3 (.D(or_13_out), .clk(clock_4_out), .Q(Am));  // open: Qn, preset, reset
  Clock clock_4 (.out(clock_4_out));
  D_Flip_Flop d_ff_4 (.D(or_14_out), .clk(clock_5_out), .Q(Ax));  // open: Qn, preset, reset
  Clock clock_5 (.out(clock_5_out));
  D_Flip_Flop d_ff_5 (.D(or_15_out), .clk(clock_6_out), .Q(ApN));  // open: Qn, preset, reset
  Clock clock_6 (.out(clock_6_out));
  D_Flip_Flop d_ff_6 (.D(or_16_out), .clk(clock_7_out), .Q(AmN));  // open: Qn, preset, reset
  Clock clock_7 (.out(clock_7_out));
  D_Flip_Flop d_ff_7 (.D(or_18_out), .clk(clock_8_out), .Q(AxN));  // open: Qn, preset, reset
  Clock clock_8 (.out(clock_8_out));
  D_Flip_Flop d_ff_8 (.D(or_19_out), .clk(clock_9_out), .Q(ApNp));  // open: Qn, preset, reset
  Clock clock_9 (.out(clock_9_out));
  D_Flip_Flop d_ff_9 (.D(or_21_out), .clk(clock_10_out), .Q(ApNx));  // open: Qn, preset, reset
  Clock clock_10 (.out(clock_10_out));
  D_Flip_Flop d_ff_10 (.D(or_23_out), .clk(clock_11_out), .Q(ApNm));  // open: Qn, preset, reset
  Clock clock_11 (.out(clock_11_out));
  D_Flip_Flop d_ff_11 (.D(or_25_out), .clk(clock_12_out), .Q(AmNp));  // open: Qn, preset, reset
  Clock clock_12 (.out(clock_12_out));
  D_Flip_Flop d_ff_12 (.D(or_27_out), .clk(clock_13_out), .Q(AmNx));  // open: Qn, preset, reset
  Clock clock_13 (.out(clock_13_out));
  D_Flip_Flop d_ff_13 (.D(or_28_out), .clk(clock_14_out), .Q(AmNm));  // open: Qn, preset, reset
  Clock clock_14 (.out(clock_14_out));

  // Notes on the sheet:
  //   R
  //   A
  //   Am
  //   Ap
  //   Ax
  //   ApN
  //   AmN
  //   AxN
  //   ApNp
  //   ApNx
  //   ApNm
  //   AmNp
  //   AmNx
  //   AmNm
  //   R
  //   A
  //   Ap
  //   Am
  //   Ax
  //   ApN
  //   AmN
  //   AxN
  //   ApNp
  //   ApNx
  //   ApNm
  //   AmNp
  //   AmNx
  //   AmNm
endmodule

module TC (
  input  [19:0] in_1,
  input  in_2,
  output [19:0] out_3
);

  wire [19:0] plus_1_out_5_2;
  wire [20:0] not_1_out;
  wire [20:20] plus_1_out_5;

  not not_1 (not_1_out[0], in_1[0]);
  not not_2 (not_1_out[1], in_1[1]);
  not not_3 (not_1_out[2], in_1[2]);
  not not_4 (not_1_out[3], in_1[3]);
  not not_5 (not_1_out[4], in_1[4]);
  not not_6 (not_1_out[5], in_1[5]);
  not not_7 (not_1_out[6], in_1[6]);
  not not_8 (not_1_out[7], in_1[7]);
  not not_9 (not_1_out[8], in_1[8]);
  not not_10 (not_1_out[9], in_1[9]);
  not not_11 (not_1_out[10], in_1[10]);
  not not_12 (not_1_out[11], in_1[11]);
  not not_13 (not_1_out[12], in_1[12]);
  not not_14 (not_1_out[13], in_1[13]);
  not not_15 (not_1_out[14], in_1[14]);
  not not_16 (not_1_out[15], in_1[15]);
  not not_17 (not_1_out[16], in_1[16]);
  not not_18 (not_1_out[17], in_1[17]);
  not not_19 (not_1_out[18], in_1[18]);
  not not_20 (not_1_out[19], in_1[19]);
  not not_21 (not_1_out[20], in_2);
  Multiplexer #(.width(20)) multiplexer_1 (.in0(in_1), .in1(plus_1_out_5_2), .out(out_3), .sel(in_2));
  plus plus_1 (.in_1(not_1_out), .in_2(21'h1), .out_5({plus_1_out_5[20], plus_1_out_5_2}));  // open: M, overFlow
endmodule
